// Logisim project 6-bit_Non-pipelined_Parallel_Unsigned_Binary_Array_Multiplier.circ as structural Verilog: 3 circuits, main circuit main
module main (
  output halt,
  output [11:0] C,
  output [5:0] O1,
  output [5:0] O2
);

  wire clock_1_out, comparator_1_eq, comparator_2_eq;
  wire [5:0] adder_1_out, divider_1_out, divider_1_rem, register_1_q, register_2_q, register_3_q,
       register_4_q;

  Clock clock_1 (.out(clock_1_out));
  Counter #(.width(12), .max('hfbf)) counter_1 (
    .clk(clock_1_out), .carry(halt), .Q(C));  // open: clr, load, up, count, D
  // Probe on adder_1_out
  // Probe on C[5:0]
  Adder #(.width(6)) adder_1 (.a(C[11:6]), .b(6'b000001), .out(adder_1_out));  // open: cin, cout
  // AND_Gate and_1 has open pins: in0=comparator_2_eq, in1=comparator_1_eq, out=open
  Divider #(.width(6)) divider_1 (
    .a(C[5:0]), .b(adder_1_out), .out(divider_1_out), .rem(divider_1_rem));  // open: upper
  // Probe on O1
  mycircuit mycircuit_1 (.A(C[5:0]), .B(adder_1_out), .Q(O1), .R(O2));
  // Probe on divider_1_out
  // Probe on divider_1_rem
  // Probe on O2
  Register #(.width(6), .trigger("falling")) register_1 (.D(O1), .clk(clock_1_out), .Q(register_1_q));  // open: en, clr
  Register #(.width(6), .trigger("falling")) register_2 (
    .D(divider_1_out), .clk(clock_1_out), .Q(register_2_q));  // open: en, clr
  Register #(.width(6), .trigger("falling")) register_3 (.D(O2), .clk(clock_1_out), .Q(register_3_q));  // open: en, clr
  Register #(.width(6), .trigger("falling")) register_4 (
    .D(divider_1_rem), .clk(clock_1_out), .Q(register_4_q));  // open: en, clr
  Comparator #(.width(6)) comparator_1 (.a(register_1_q), .b(register_2_q), .eq(comparator_1_eq));  // open: gt, lt
  Comparator #(.width(6)) comparator_2 (.a(register_3_q), .b(register_4_q), .eq(comparator_2_eq));  // open: gt, lt

  // Notes on the sheet:
  //   Attention, votre version de Logisim
  //   ne contient pas de tracker. Si vous
  //   enregistrez votre projet, toutes les
  //   informations du tracker seront
  //   définitivement effacées.
endmodule

module mycircuit (
  input  [5:0] A,
  input  [5:0] B,
  output [5:0] Q,
  output [5:0] R
);

  wire pu_2_cout, pu_2_r, pu_4_cout, pu_4_r, pu_5_cout, pu_5_r, pu_7_cout, pu_7_r, pu_8_cout, pu_8_r,
       pu_9_cout, pu_9_r, pu_11_cout, pu_11_r, pu_12_cout, pu_12_r, pu_13_cout, pu_13_r, pu_14_cout, pu_14_r,
       pu_16_cout, pu_16_r, pu_17_cout, pu_17_r, pu_18_cout, pu_18_r, pu_19_cout, pu_19_r, pu_20_cout,
       pu_20_r, pu_22_cout, pu_22_r, pu_23_cout, pu_23_r, pu_24_cout, pu_24_r, pu_25_cout, pu_25_r,
       pu_26_cout, pu_27_cout, pu_27_r, pu_28_cout, pu_28_r, pu_29_cout, pu_29_r, pu_30_cout, pu_31_cout,
       pu_31_r, pu_32_cout, pu_32_r, pu_33_cout, pu_34_cout, pu_34_r, pu_35_cout, pu_36_cout;

  PU pu_1 (.A(1'b0), .B(B[5]), .Cin(pu_2_cout), .S(Q[5]), .Cout(Q[5]));  // open: R
  PU pu_2 (.A(1'b0), .B(B[4]), .Cin(pu_4_cout), .S(Q[5]), .R(pu_2_r), .Cout(pu_2_cout));
  PU pu_3 (.A(pu_2_r), .B(B[5]), .Cin(pu_5_cout), .S(Q[4]), .Cout(Q[4]));  // open: R
  PU pu_4 (.A(1'b0), .B(B[3]), .Cin(pu_7_cout), .S(Q[5]), .R(pu_4_r), .Cout(pu_4_cout));
  PU pu_5 (.A(pu_4_r), .B(B[4]), .Cin(pu_8_cout), .S(Q[4]), .R(pu_5_r), .Cout(pu_5_cout));
  PU pu_6 (.A(pu_5_r), .B(B[5]), .Cin(pu_9_cout), .S(Q[3]), .Cout(Q[3]));  // open: R
  PU pu_7 (.A(1'b0), .B(B[2]), .Cin(pu_11_cout), .S(Q[5]), .R(pu_7_r), .Cout(pu_7_cout));
  PU pu_8 (.A(pu_7_r), .B(B[3]), .Cin(pu_12_cout), .S(Q[4]), .R(pu_8_r), .Cout(pu_8_cout));
  PU pu_9 (.A(pu_8_r), .B(B[4]), .Cin(pu_13_cout), .S(Q[3]), .R(pu_9_r), .Cout(pu_9_cout));
  PU pu_10 (.A(pu_9_r), .B(B[5]), .Cin(pu_14_cout), .S(Q[2]), .Cout(Q[2]));  // open: R
  PU pu_11 (.A(1'b0), .B(B[1]), .Cin(pu_16_cout), .S(Q[5]), .R(pu_11_r), .Cout(pu_11_cout));
  PU pu_12 (.A(pu_11_r), .B(B[2]), .Cin(pu_17_cout), .S(Q[4]), .R(pu_12_r), .Cout(pu_12_cout));
  PU pu_13 (.A(pu_12_r), .B(B[3]), .Cin(pu_18_cout), .S(Q[3]), .R(pu_13_r), .Cout(pu_13_cout));
  PU pu_14 (.A(pu_13_r), .B(B[4]), .Cin(pu_19_cout), .S(Q[2]), .R(pu_14_r), .Cout(pu_14_cout));
  PU pu_15 (.A(pu_14_r), .B(B[5]), .Cin(pu_20_cout), .S(Q[1]), .Cout(Q[1]));  // open: R
  PU pu_16 (.A(A[5]), .B(B[0]), .Cin(1'b1), .S(Q[5]), .R(pu_16_r), .Cout(pu_16_cout));
  PU pu_17 (.A(pu_16_r), .B(B[1]), .Cin(pu_22_cout), .S(Q[4]), .R(pu_17_r), .Cout(pu_17_cout));
  PU pu_18 (.A(pu_17_r), .B(B[2]), .Cin(pu_23_cout), .S(Q[3]), .R(pu_18_r), .Cout(pu_18_cout));
  PU pu_19 (.A(pu_18_r), .B(B[3]), .Cin(pu_24_cout), .S(Q[2]), .R(pu_19_r), .Cout(pu_19_cout));
  PU pu_20 (.A(pu_19_r), .B(B[4]), .Cin(pu_25_cout), .S(Q[1]), .R(pu_20_r), .Cout(pu_20_cout));
  PU pu_21 (.A(pu_20_r), .B(B[5]), .Cin(pu_26_cout), .S(Q[0]), .R(R[5]), .Cout(Q[0]));
  PU pu_22 (.A(A[4]), .B(B[0]), .Cin(1'b1), .S(Q[4]), .R(pu_22_r), .Cout(pu_22_cout));
  PU pu_23 (.A(pu_22_r), .B(B[1]), .Cin(pu_27_cout), .S(Q[3]), .R(pu_23_r), .Cout(pu_23_cout));
  PU pu_24 (.A(pu_23_r), .B(B[2]), .Cin(pu_28_cout), .S(Q[2]), .R(pu_24_r), .Cout(pu_24_cout));
  PU pu_25 (.A(pu_24_r), .B(B[3]), .Cin(pu_29_cout), .S(Q[1]), .R(pu_25_r), .Cout(pu_25_cout));
  PU pu_26 (.A(pu_25_r), .B(B[4]), .Cin(pu_30_cout), .S(Q[0]), .R(R[4]), .Cout(pu_26_cout));
  PU pu_27 (.A(A[3]), .B(B[0]), .Cin(1'b1), .S(Q[3]), .R(pu_27_r), .Cout(pu_27_cout));
  PU pu_28 (.A(pu_27_r), .B(B[1]), .Cin(pu_31_cout), .S(Q[2]), .R(pu_28_r), .Cout(pu_28_cout));
  PU pu_29 (.A(pu_28_r), .B(B[2]), .Cin(pu_32_cout), .S(Q[1]), .R(pu_29_r), .Cout(pu_29_cout));
  PU pu_30 (.A(pu_29_r), .B(B[3]), .Cin(pu_33_cout), .S(Q[0]), .R(R[3]), .Cout(pu_30_cout));
  PU pu_31 (.A(A[2]), .B(B[0]), .Cin(1'b1), .S(Q[2]), .R(pu_31_r), .Cout(pu_31_cout));
  PU pu_32 (.A(pu_31_r), .B(B[1]), .Cin(pu_34_cout), .S(Q[1]), .R(pu_32_r), .Cout(pu_32_cout));
  PU pu_33 (.A(pu_32_r), .B(B[2]), .Cin(pu_35_cout), .S(Q[0]), .R(R[2]), .Cout(pu_33_cout));
  PU pu_34 (.A(A[1]), .B(B[0]), .Cin(1'b1), .S(Q[1]), .R(pu_34_r), .Cout(pu_34_cout));
  PU pu_35 (.A(pu_34_r), .B(B[1]), .Cin(pu_36_cout), .S(Q[0]), .R(R[1]), .Cout(pu_35_cout));
  PU pu_36 (.A(A[0]), .B(B[0]), .Cin(1'b1), .S(Q[0]), .R(R[0]), .Cout(pu_36_cout));

  // Notes on the sheet:
  //   Attention, votre version de Logisim
  //   ne contient pas de tracker. Si vous
  //   enregistrez votre projet, toutes les
  //   informations du tracker seront
  //   définitivement effacées.
endmodule

module PU (
  input  A,
  input  B,
  input  Cin,
  input  S,
  output R,
  output Cout
);

  wire adder_1_out, not_1_out;

  not not_1 (not_1_out, B);
  Adder #(.width(1)) adder_1 (.a(A), .b(not_1_out), .out(adder_1_out), .cin(Cin), .cout(Cout));
  Multiplexer #(.enable("false")) multiplexer_1 (.in0(A), .in1(adder_1_out), .out(R), .sel(S));

  // Notes on the sheet:
  //   Attention, votre version de Logisim
  //   ne contient pas de tracker. Si vous
  //   enregistrez votre projet, toutes les
  //   informations du tracker seront
  //   définitivement effacées.
endmodule
