// Logisim project 6-bit_Non-pipelined_Parallel_Unsigned_Binary_Divider.circ as structural Verilog: 4 circuits, main circuit main
module main (
  output halt,
  output [11:0] C,
  output [11:0] O
);

  wire clock_1_out;
  wire [11:0] bit_extender_1_out, bit_extender_2_out, multiplier_1_out, register_1_q, register_2_q;

  Clock clock_1 (.out(clock_1_out));
  Counter #(.width(12), .max('hfff)) counter_1 (
    .clk(clock_1_out), .carry(halt), .Q(C));  // open: clr, load, up, count, D
  // Probe on C[11:6]
  // Probe on C[5:0]
  assign bit_extender_1_out = {{6{1'b0}}, C[5:0]};  // Bit_Extender bit_extender_1
  assign bit_extender_2_out = {{6{1'b0}}, C[11:6]};  // Bit_Extender bit_extender_2
  // Probe on O
  mycircuit mycircuit_1 (.A(C[5:0]), .B(C[11:6]), .P(O));
  // Probe on multiplier_1_out
  Multiplier #(.width(12)) multiplier_1 (
    .a(bit_extender_1_out), .b(bit_extender_2_out), .out(multiplier_1_out));  // open: cin, cout
  Register #(.width(12), .trigger("falling")) register_1 (.D(O), .clk(clock_1_out), .Q(register_1_q));  // open: en, clr
  Register #(.width(12), .trigger("falling")) register_2 (
    .D(multiplier_1_out), .clk(clock_1_out), .Q(register_2_q));  // open: en, clr
  Comparator #(.width(12)) comparator_1 (.a(register_1_q), .b(register_2_q));  // open: gt, eq, lt

  // Notes on the sheet:
  //   Attention, votre version de Logisim
  //   ne contient pas de tracker. Si vous
  //   enregistrez votre projet, toutes les
  //   informations du tracker seront
  //   définitivement effacées.
endmodule

module mycircuit (
  input  [5:0] A,
  input  [5:0] B,
  output [11:0] P
);

  wire A0B1, A0B2, A0B3, A0B4, A0B5, A1_cout, A1B0, A1B1, A1B2, A1B3, A1B4, A1B5, A2_cout, A2_sum, A2B0,
       A2B1, A2B2, A2B3, A2B4, A2B5, A3_cout, A3_sum, A3B0, A3B1, A3B2, A3B3, A3B4, A3B5, A4_cout, A4_sum,
       A4B0, A4B1, A4B2, A4B3, A4B4, A4B5, A5_cout, A5_sum, A5B0, A5B1, A5B2, A5B3, A5B4, A5B5, A6_cout,
       A6_sum, A7_cout, A7_sum, A8_cout, A8_sum, A9_cout, A9_s, A13_cout, A14_cout, A14_sum, A15_cout,
       A15_sum, A16_cout, A16_sum, A17_cout, A17_sum, A18_cout, A18_sum, A19_cout, A19_s, A20_cout, A20_s,
       A21_s, C10, C11, C12, C21, C22, C23, C24, C25, C26, C27, C28, C29, S10, S11, S12, S23, S24, S25, S26,
       S27, S28, S29;

  HA A12 (.A(A2B4), .B(A1B5), .S(S12), .Cout(C12));
  FA A11 (.A(A2B3), .B(A1B4), .Cin(A0B5), .Sum(S11), .Cout(C11));
  HA A10 (.A(A1B3), .B(A0B4), .S(S10), .Cout(C10));
  HA A21 (.A(A9_cout), .B(A5B5), .S(A21_s), .Cout(C21));
  HA A29 (.A(A20_cout), .B(A21_s), .S(S29), .Cout(C29));
  Adder adder_1 (
    .a({C29, C28, C27, C26, C25, C24, C23, C22}), .b({C21, S29, S28, S27, S26, S25, S24, S23}), .out(P[11:4]));  // open: cin, cout
  HA A9 (.A(A5B4), .B(A4B5), .S(A9_s), .Cout(A9_cout));
  HA A20 (.A(A8_cout), .B(A9_s), .S(A20_s), .Cout(A20_cout));
  HA A28 (.A(A19_cout), .B(A20_s), .S(S28), .Cout(C28));
  FA A8 (.A(A5B3), .B(A4B4), .Cin(A3B5), .Sum(A8_sum), .Cout(A8_cout));
  HA A19 (.A(A7_cout), .B(A8_sum), .S(A19_s), .Cout(A19_cout));
  HA A27 (.A(A18_cout), .B(A19_s), .S(S27), .Cout(C27));
  FA A7 (.A(A5B2), .B(A4B3), .Cin(A3B4), .Sum(A7_sum), .Cout(A7_cout));
  FA A18 (.A(A6_cout), .B(A7_sum), .Cin(C12), .Sum(A18_sum), .Cout(A18_cout));
  FA A26 (.A(A17_cout), .B(A18_sum), .Cin(A2B5), .Sum(S26), .Cout(C26));
  FA A6 (.A(A5B1), .B(A4B2), .Cin(A3B3), .Sum(A6_sum), .Cout(A6_cout));
  FA A17 (.A(A5_cout), .B(A6_sum), .Cin(C11), .Sum(A17_sum), .Cout(A17_cout));
  FA A25 (.A(A16_cout), .B(A17_sum), .Cin(S12), .Sum(S25), .Cout(C25));
  FA A5 (.A(A5B0), .B(A4B1), .Cin(A3B2), .Sum(A5_sum), .Cout(A5_cout));
  FA A16 (.A(A4_cout), .B(A5_sum), .Cin(C10), .Sum(A16_sum), .Cout(A16_cout));
  FA A24 (.A(A15_cout), .B(A16_sum), .Cin(S11), .Sum(S24), .Cout(C24));
  FA A4 (.A(A4B0), .B(A3B1), .Cin(A2B2), .Sum(A4_sum), .Cout(A4_cout));
  FA A15 (.A(A3_cout), .B(A4_sum), .Cin(S10), .Sum(A15_sum), .Cout(A15_cout));
  HA A23 (.A(A14_cout), .B(A15_sum), .S(S23), .Cout(C23));
  FA A3 (.A(A3B0), .B(A2B1), .Cin(A1B2), .Sum(A3_sum), .Cout(A3_cout));
  FA A14 (.A(A2_cout), .B(A3_sum), .Cin(A0B3), .Sum(A14_sum), .Cout(A14_cout));
  HA A22 (.A(A13_cout), .B(A14_sum), .S(P[3]), .Cout(C22));
  FA A2 (.A(A2B0), .B(A1B1), .Cin(A0B2), .Sum(A2_sum), .Cout(A2_cout));
  HA A13 (.A(A1_cout), .B(A2_sum), .S(P[2]), .Cout(A13_cout));
  HA A1 (.A(A1B0), .B(A0B1), .S(P[1]), .Cout(A1_cout));
  and and_1 (A5B5, B[5], A[5]);
  and and_2 (A5B4, B[4], A[5]);
  and and_3 (A4B5, B[5], A[4]);
  and and_4 (A5B3, B[3], A[5]);
  and and_5 (A4B4, B[4], A[4]);
  and and_6 (A3B5, B[5], A[3]);
  and and_7 (A5B2, B[2], A[5]);
  and and_8 (A4B3, B[3], A[4]);
  and and_9 (A3B4, B[4], A[3]);
  and and_10 (A2B5, B[5], A[2]);
  and and_11 (A5B1, B[1], A[5]);
  and and_12 (A4B2, B[2], A[4]);
  and and_13 (A3B3, B[3], A[3]);
  and and_14 (A2B4, B[4], A[2]);
  and and_15 (A1B5, B[5], A[1]);
  and and_16 (A5B0, B[0], A[5]);
  and and_17 (A4B1, B[1], A[4]);
  and and_18 (A3B2, B[2], A[3]);
  and and_19 (A2B3, B[3], A[2]);
  and and_20 (A1B4, B[4], A[1]);
  and and_21 (A0B5, B[5], A[0]);
  and and_22 (A4B0, B[0], A[4]);
  and and_23 (A3B1, B[1], A[3]);
  and and_24 (A2B2, B[2], A[2]);
  and and_25 (A1B3, B[3], A[1]);
  and and_26 (A0B4, B[4], A[0]);
  and and_27 (A3B0, B[0], A[3]);
  and and_28 (A2B1, B[1], A[2]);
  and and_29 (A1B2, B[2], A[1]);
  and and_30 (A0B3, B[3], A[0]);
  and and_31 (A2B0, B[0], A[2]);
  and and_32 (A1B1, B[1], A[1]);
  and and_33 (A0B2, B[2], A[0]);
  and and_34 (A1B0, B[0], A[1]);
  and and_35 (A0B1, B[1], A[0]);
  and and_36 (P[0], B[0], A[0]);

  // Other names for the same wires on the sheet: A0B0 = P[0]

  // Notes on the sheet:
  //   Attention, votre version de Logisim
  //   ne contient pas de tracker. Si vous
  //   enregistrez votre projet, toutes les
  //   informations du tracker seront
  //   définitivement effacées.
endmodule

module HA (
  input  A,
  input  B,
  output S,
  output Cout
);

  xor xor_1 (S, A, B);
  and and_1 (Cout, A, B);

  // Notes on the sheet:
  //   Attention, votre version de Logisim
  //   ne contient pas de tracker. Si vous
  //   enregistrez votre projet, toutes les
  //   informations du tracker seront
  //   définitivement effacées.
endmodule

module FA (
  input  A,
  input  B,
  input  Cin,
  output Sum,
  output Cout
);

  wire and_1_out, and_2_out, xor_1_out;

  and and_1 (and_1_out, A, B);
  and and_2 (and_2_out, xor_1_out, Cin);
  or or_1 (Cout, and_1_out, and_2_out);
  xor xor_1 (xor_1_out, A, B);
  xor xor_2 (Sum, xor_1_out, Cin);

  // Notes on the sheet:
  //   Attention, votre version de Logisim
  //   ne contient pas de tracker. Si vous
  //   enregistrez votre projet, toutes les
  //   informations du tracker seront
  //   définitivement effacées.
endmodule
