// Logisim project 6-bit_Non-pipelined_Wallace_Tree_Unsigned_Multiplier.circ as structural Verilog: 4 circuits, main circuit main
module main (
  output halt,
  output [11:0] C,
  output [11:0] O
);

  wire clock_1_out;
  wire [11:0] bit_extender_1_out, bit_extender_2_out, multiplier_1_out, register_1_q, register_2_q;

  Clock clock_1 (.out(clock_1_out));
  Counter #(.width(12), .max('hfff)) counter_1 (
    .clk(clock_1_out), .carry(halt), .Q(C));  // open: clr, load, up, count, D
  // Probe on C[11:6]
  // Probe on C[5:0]
  assign bit_extender_1_out = {{6{1'b0}}, C[5:0]};  // Bit_Extender bit_extender_1
  assign bit_extender_2_out = {{6{1'b0}}, C[11:6]};  // Bit_Extender bit_extender_2
  // Probe on O
  mycircuit mycircuit_1 (.A(C[5:0]), .B(C[11:6]), .P(O));
  // Probe on multiplier_1_out
  Multiplier #(.width(12)) multiplier_1 (
    .a(bit_extender_1_out), .b(bit_extender_2_out), .out(multiplier_1_out));  // open: cin, cout
  Register #(.width(12), .trigger("falling")) register_1 (.D(O), .clk(clock_1_out), .Q(register_1_q));  // open: en, clr
  Register #(.width(12), .trigger("falling")) register_2 (
    .D(multiplier_1_out), .clk(clock_1_out), .Q(register_2_q));  // open: en, clr
  Comparator #(.width(12)) comparator_1 (.a(register_1_q), .b(register_2_q));  // open: gt, eq, lt

  // Notes on the sheet:
  //   Attention, votre version de Logisim
  //   ne contient pas de tracker. Si vous
  //   enregistrez votre projet, toutes les
  //   informations du tracker seront
  //   définitivement effacées.
endmodule

module mycircuit (
  input  [5:0] A,
  input  [5:0] B,
  output [11:0] P
);

  wire and_1_out, and_2_out, and_3_out, and_4_out, and_5_out, and_6_out, and_7_out, and_8_out, and_9_out,
       and_10_out, and_11_out, and_12_out, and_13_out, and_14_out, and_15_out, and_16_out, and_17_out,
       and_18_out, and_19_out, and_20_out, and_21_out, and_22_out, and_23_out, and_24_out, and_25_out,
       and_26_out, and_27_out, and_28_out, and_29_out, and_30_out, and_31_out, and_32_out, and_33_out,
       and_34_out, and_35_out, fa_2_cout, fa_2_sum, fa_3_cout, fa_4_cout, fa_4_sum, fa_5_cout, fa_5_sum,
       fa_6_cout, fa_7_cout, fa_7_sum, fa_8_cout, fa_8_sum, fa_9_cout, fa_9_sum, fa_10_cout, fa_11_cout,
       fa_11_sum, fa_12_cout, fa_12_sum, fa_13_cout, fa_13_sum, fa_14_cout, fa_14_sum, fa_15_cout,
       fa_16_cout, fa_16_sum, fa_17_cout, fa_17_sum, fa_18_cout, fa_18_sum, fa_19_cout, fa_19_sum,
       fa_20_cout, fa_20_sum, fa_21_cout, fa_21_sum, fa_22_cout, fa_22_sum, fa_23_cout, fa_23_sum,
       fa_24_cout, fa_24_sum, ha_1_cout, ha_1_s, ha_2_cout, ha_3_cout, ha_4_cout, ha_5_cout, ha_6_cout;

  and and_1 (and_1_out, B[5], A[5]);
  FA fa_1 (.A(and_1_out), .B(fa_2_cout), .Cin(fa_3_cout), .Cout(P[11]), .Sum(P[10]));
  and and_2 (and_2_out, B[4], A[5]);
  FA fa_2 (.A(and_2_out), .B(fa_4_cout), .Cin(fa_5_cout), .Cout(fa_2_cout), .Sum(fa_2_sum));
  and and_3 (and_3_out, B[5], A[4]);
  FA fa_3 (.A(and_3_out), .B(fa_2_sum), .Cin(fa_6_cout), .Cout(fa_3_cout), .Sum(P[9]));
  and and_4 (and_4_out, B[3], A[5]);
  FA fa_4 (.A(and_4_out), .B(fa_7_cout), .Cin(fa_8_cout), .Cout(fa_4_cout), .Sum(fa_4_sum));
  and and_5 (and_5_out, B[4], A[4]);
  FA fa_5 (.A(and_5_out), .B(fa_4_sum), .Cin(fa_9_cout), .Cout(fa_5_cout), .Sum(fa_5_sum));
  and and_6 (and_6_out, B[5], A[3]);
  FA fa_6 (.A(and_6_out), .B(fa_5_sum), .Cin(fa_10_cout), .Cout(fa_6_cout), .Sum(P[8]));
  and and_7 (and_7_out, B[2], A[5]);
  FA fa_7 (.A(and_7_out), .B(ha_1_cout), .Cin(fa_11_cout), .Cout(fa_7_cout), .Sum(fa_7_sum));
  and and_8 (and_8_out, B[3], A[4]);
  FA fa_8 (.A(and_8_out), .B(fa_7_sum), .Cin(fa_12_cout), .Cout(fa_8_cout), .Sum(fa_8_sum));
  and and_9 (and_9_out, B[4], A[3]);
  FA fa_9 (.A(and_9_out), .B(fa_8_sum), .Cin(fa_13_cout), .Cout(fa_9_cout), .Sum(fa_9_sum));
  and and_10 (and_10_out, B[5], A[2]);
  FA fa_10 (.A(and_10_out), .B(fa_9_sum), .Cin(fa_15_cout), .Cout(fa_10_cout), .Sum(P[7]));
  and and_11 (and_11_out, B[1], A[5]);
  HA ha_1 (.A(and_11_out), .B(fa_14_cout), .Cout(ha_1_cout), .S(ha_1_s));
  and and_12 (and_12_out, B[2], A[4]);
  FA fa_11 (.A(and_12_out), .B(ha_1_s), .Cin(fa_16_cout), .Cout(fa_11_cout), .Sum(fa_11_sum));
  and and_13 (and_13_out, B[3], A[3]);
  FA fa_12 (.A(and_13_out), .B(fa_11_sum), .Cin(fa_17_cout), .Cout(fa_12_cout), .Sum(fa_12_sum));
  and and_14 (and_14_out, B[4], A[2]);
  FA fa_13 (.A(and_14_out), .B(fa_12_sum), .Cin(fa_18_cout), .Cout(fa_13_cout), .Sum(fa_13_sum));
  and and_15 (and_15_out, B[0], A[5]);
  and and_16 (and_16_out, B[1], A[4]);
  FA fa_14 (.A(and_16_out), .B(and_15_out), .Cin(fa_19_cout), .Cout(fa_14_cout), .Sum(fa_14_sum));
  and and_17 (and_17_out, B[5], A[1]);
  FA fa_15 (.A(and_17_out), .B(fa_13_sum), .Cin(ha_2_cout), .Cout(fa_15_cout), .Sum(P[6]));
  and and_18 (and_18_out, B[0], A[4]);
  and and_19 (and_19_out, B[2], A[3]);
  FA fa_16 (.A(and_19_out), .B(fa_14_sum), .Cin(fa_20_cout), .Cout(fa_16_cout), .Sum(fa_16_sum));
  and and_20 (and_20_out, B[3], A[2]);
  FA fa_17 (.A(and_20_out), .B(fa_16_sum), .Cin(fa_21_cout), .Cout(fa_17_cout), .Sum(fa_17_sum));
  and and_21 (and_21_out, B[4], A[1]);
  FA fa_18 (.A(and_21_out), .B(fa_17_sum), .Cin(ha_3_cout), .Cout(fa_18_cout), .Sum(fa_18_sum));
  and and_22 (and_22_out, B[5], A[0]);
  HA ha_2 (.A(and_22_out), .B(fa_18_sum), .Cout(ha_2_cout), .S(P[5]));
  and and_23 (and_23_out, B[1], A[3]);
  FA fa_19 (.A(and_23_out), .B(and_18_out), .Cin(fa_22_cout), .Cout(fa_19_cout), .Sum(fa_19_sum));
  and and_24 (and_24_out, B[2], A[2]);
  FA fa_20 (.A(and_24_out), .B(fa_19_sum), .Cin(fa_23_cout), .Cout(fa_20_cout), .Sum(fa_20_sum));
  and and_25 (and_25_out, B[3], A[1]);
  FA fa_21 (.A(and_25_out), .B(fa_20_sum), .Cin(ha_4_cout), .Cout(fa_21_cout), .Sum(fa_21_sum));
  and and_26 (and_26_out, B[0], A[3]);
  and and_27 (and_27_out, B[4], A[0]);
  HA ha_3 (.A(and_27_out), .B(fa_21_sum), .Cout(ha_3_cout), .S(P[4]));
  and and_28 (and_28_out, B[1], A[2]);
  FA fa_22 (.A(and_28_out), .B(and_26_out), .Cin(fa_24_cout), .Cout(fa_22_cout), .Sum(fa_22_sum));
  and and_29 (and_29_out, B[2], A[1]);
  FA fa_23 (.A(and_29_out), .B(fa_22_sum), .Cin(ha_5_cout), .Cout(fa_23_cout), .Sum(fa_23_sum));
  and and_30 (and_30_out, B[3], A[0]);
  HA ha_4 (.A(and_30_out), .B(fa_23_sum), .Cout(ha_4_cout), .S(P[3]));
  and and_31 (and_31_out, B[0], A[2]);
  and and_32 (and_32_out, B[1], A[1]);
  FA fa_24 (.A(and_32_out), .B(and_31_out), .Cin(ha_6_cout), .Cout(fa_24_cout), .Sum(fa_24_sum));
  and and_33 (and_33_out, B[2], A[0]);
  HA ha_5 (.A(and_33_out), .B(fa_24_sum), .Cout(ha_5_cout), .S(P[2]));
  and and_34 (and_34_out, B[0], A[1]);
  and and_35 (and_35_out, B[1], A[0]);
  HA ha_6 (.A(and_35_out), .B(and_34_out), .Cout(ha_6_cout), .S(P[1]));
  and and_36 (P[0], B[0], A[0]);

  // Notes on the sheet:
  //   Attention, votre version de Logisim
  //   ne contient pas de tracker. Si vous
  //   enregistrez votre projet, toutes les
  //   informations du tracker seront
  //   définitivement effacées.
endmodule

module HA (
  input  A,
  input  B,
  output Cout,
  output S
);

  and and_1 (Cout, A, B);
  xor xor_1 (S, A, B);

  // Notes on the sheet:
  //   Attention, votre version de Logisim
  //   ne contient pas de tracker. Si vous
  //   enregistrez votre projet, toutes les
  //   informations du tracker seront
  //   définitivement effacées.
endmodule

module FA (
  input  A,
  input  B,
  input  Cin,
  output Cout,
  output Sum
);

  wire and_1_out, and_2_out, xor_1_out;

  and and_1 (and_1_out, A, B);
  and and_2 (and_2_out, xor_1_out, Cin);
  or or_1 (Cout, and_1_out, and_2_out);
  xor xor_1 (xor_1_out, A, B);
  xor xor_2 (Sum, xor_1_out, Cin);

  // Notes on the sheet:
  //   Attention, votre version de Logisim
  //   ne contient pas de tracker. Si vous
  //   enregistrez votre projet, toutes les
  //   informations du tracker seront
  //   définitivement effacées.
endmodule
