// Logisim project 6-bit_Pipelined_Parallel_Unsigned_Binary_Array_Multiplier.circ as structural Verilog: 5 circuits, main circuit main
module main (
  output halt,
  output [5:0] A,
  output [5:0] B,
  output [11:0] P
);

  wire clock_1_out, comparator_1_eq, d_ff_1_q;
  wire [11:0] bit_extender_1_out, bit_extender_2_out, multiplier_1_out, random_1_out;

  Counter #(.width(12), .max('hfff)) counter_1 (.clk(clock_1_out), .carry(halt));  // open: clr, load, up, count, D, Q
  Clock clock_1 (.out(clock_1_out));
  Random #(.width(12)) random_1 (.next(d_ff_1_q), .clk(clock_1_out), .out(random_1_out));  // open: clr
  // Probe on random_1_out[5:0]
  // Probe on random_1_out[11:6]
  RAM #(.addrWidth(12), .dataWidth(1), .trigger("falling"), .databus("bibus")) ram_1 (
    .addr(random_1_out), .we(d_ff_1_q), .clk(clock_1_out), .din(1'b1));  // open: oe, dout
  // Probe on A
  mycircuit mycircuit_1 (
    .A(random_1_out[5:0]), .B(random_1_out[11:6]), .CK(clock_1_out), .WE(d_ff_1_q), .AO(A), .BO(B), .P(P));
  // Probe on B
  assign bit_extender_1_out = {{6{1'b0}}, A};  // Bit_Extender bit_extender_1
  assign bit_extender_2_out = {{6{1'b0}}, B};  // Bit_Extender bit_extender_2
  Multiplier #(.width(12)) multiplier_1 (
    .a(bit_extender_1_out), .b(bit_extender_2_out), .out(multiplier_1_out));  // open: cin, cout
  // Probe on P
  Comparator #(.width(12)) comparator_1 (.a(P), .b(multiplier_1_out), .eq(comparator_1_eq));  // open: gt, lt
  // Probe on multiplier_1_out
  D_Flip_Flop #(.trigger("falling")) d_ff_1 (
    .D(comparator_1_eq), .clk(clock_1_out), .Q(d_ff_1_q));  // open: Qn, preset, reset

  // Notes on the sheet:
  //   Attention, votre version de Logisim
  //   ne contient pas de tracker. Si vous
  //   enregistrez votre projet, toutes les
  //   informations du tracker seront
  //   définitivement effacées.
endmodule

module mycircuit (
  input  [5:0] A,
  input  [5:0] B,
  input  CK,
  input  WE,
  output [5:0] AO,
  output [5:0] BO,
  output [11:0] P
);

  wire A0B2, A0B3, A0B4, A0B5, A1B2, A1B3, A1B4, A1B5, A2B2, A2B3, A2B4, A2B5, A3B2, A3B3, A3B4, A3B5, A4B2,
       A4B3, A4B4, A4B5, A5B2, A5B3, A5B4, A5B5, and_1_out, and_2_out, and_3_out, and_4_out, and_5_out,
       and_6_out, and_7_out, and_8_out, and_9_out, and_10_out, and_11_out, and_12_out, and_13_out,
       and_14_out, and_15_out, and_16_out, and_17_out, and_18_out, and_19_out, and_20_out, and_21_out,
       and_22_out, and_23_out, and_24_out, and_25_out, and_26_out, and_27_out, and_28_out, and_29_out,
       and_30_out, and_31_out, and_32_out, and_33_out, and_34_out, and_35_out, and_36_out, fa_1_cout,
       fa_1_sum, fa_2_cout, fa_2_sum, fa_3_cout, fa_3_sum, fa_4_cout, fa_4_sum, fa_5_cout, fa_5_sum,
       fa_6_cout, fa_6_sum, fa_7_cout, fa_7_sum, fa_8_cout, fa_8_sum, fa_9_cout, fa_9_sum, fa_10_cout,
       fa_10_sum, fa_11_cout, fa_11_sum, fa_12_cout, fa_12_sum, fa_13_cout, fa_13_sum, fa_14_cout, fa_14_sum,
       fa_15_cout, fa_15_sum, fa_16_cout, fa_16_sum, fa_17_cout, fa_17_sum, fa_18_cout, fa_18_sum,
       fa_19_cout, fa_19_sum, fa_20_cout, fa_20_sum, fa_21_cout, fa_21_sum, fa_22_cout, fa_22_sum,
       fa_23_cout, fa_23_sum, fa_24_cout, fa_24_sum, ha_1_cout, ha_1_s, ha_2_cout, ha_2_s, ha_3_cout, ha_3_s,
       ha_4_cout, ha_4_s, ha_5_cout, ha_5_s, ha_6_cout, ha_6_s, reg1bit_2_q, reg1bit_4_q, reg1bit_5_q,
       reg1bit_7_q, reg1bit_8_q, reg1bit_9_q, reg1bit_11_q, reg1bit_12_q, reg1bit_13_q, reg1bit_14_q,
       reg1bit_15_q, reg1bit_16_q, reg1bit_17_q, reg1bit_18_q, reg1bit_19_q, reg1bit_20_q, reg1bit_21_q,
       reg1bit_22_q, reg1bit_24_q, reg1bit_26_q, reg1bit_27_q, reg1bit_29_q, reg1bit_30_q, reg1bit_31_q,
       reg1bit_33_q, reg1bit_34_q, reg1bit_35_q, reg1bit_36_q, reg1bit_37_q, reg1bit_38_q, reg1bit_39_q,
       reg1bit_40_q, reg1bit_41_q, reg1bit_42_q, reg1bit_43_q, reg1bit_44_q, reg1bit_45_q, reg1bit_46_q,
       reg1bit_47_q, reg1bit_48_q, reg1bit_49_q, reg1bit_50_q, reg1bit_51_q, reg1bit_52_q, reg1bit_53_q,
       reg1bit_54_q, reg1bit_55_q, reg1bit_56_q, reg1bit_58_q, reg1bit_60_q, reg1bit_61_q, reg1bit_63_q,
       reg1bit_64_q, reg1bit_65_q, reg1bit_67_q, reg1bit_68_q, reg1bit_69_q, reg1bit_70_q, reg1bit_71_q,
       reg1bit_72_q, reg1bit_73_q, reg1bit_74_q, reg1bit_75_q, reg1bit_76_q, reg1bit_77_q, reg1bit_78_q,
       reg1bit_80_q, reg1bit_82_q, reg1bit_83_q, reg1bit_85_q, reg1bit_86_q, reg1bit_87_q, reg1bit_102_q,
       reg1bit_104_q, reg1bit_105_q, reg1bit_107_q, reg1bit_108_q, reg1bit_109_q, reg1bit_113_q,
       reg1bit_115_q, reg1bit_116_q, reg1bit_118_q, reg1bit_119_q, reg1bit_120_q, reg1bit_122_q,
       reg1bit_124_q, reg1bit_125_q, reg1bit_127_q, reg1bit_128_q, reg1bit_129_q, reg1bit_130_q,
       reg1bit_131_q, reg1bit_133_q, reg1bit_134_q, reg1bit_135_q, reg1bit_137_q, reg1bit_138_q,
       reg1bit_139_q, reg1bit_140_q, reg1bit_141_q, reg1bit_143_q, reg1bit_144_q, reg1bit_145_q,
       reg1bit_146_q, reg1bit_147_q, reg1bit_149_q, reg1bit_150_q, reg1bit_151_q, reg1bit_152_q,
       reg1bit_153_q, reg1bit_154_q, reg1bit_156_q, reg1bit_157_q, reg1bit_158_q, reg1bit_160_q,
       reg1bit_161_q, reg1bit_162_q, reg1bit_163_q, reg1bit_165_q, reg1bit_166_q, reg1bit_167_q,
       reg1bit_169_q;

  and and_1 (and_1_out, B[2], A[5]);
  reg1bit reg1bit_1 (.D(and_1_out), .WE(WE), .CK(CK), .Q(A5B2));
  and and_2 (and_2_out, B[3], A[5]);
  reg1bit reg1bit_2 (.D(and_2_out), .WE(WE), .CK(CK), .Q(reg1bit_2_q));
  reg1bit reg1bit_3 (.D(reg1bit_2_q), .WE(WE), .CK(CK), .Q(A5B3));
  and and_3 (and_3_out, B[4], A[5]);
  reg1bit reg1bit_4 (.D(and_3_out), .WE(WE), .CK(CK), .Q(reg1bit_4_q));
  reg1bit reg1bit_5 (.D(reg1bit_4_q), .WE(WE), .CK(CK), .Q(reg1bit_5_q));
  reg1bit reg1bit_6 (.D(reg1bit_5_q), .WE(WE), .CK(CK), .Q(A5B4));
  and and_4 (and_4_out, B[5], A[5]);
  reg1bit reg1bit_7 (.D(and_4_out), .WE(WE), .CK(CK), .Q(reg1bit_7_q));
  reg1bit reg1bit_8 (.D(reg1bit_7_q), .WE(WE), .CK(CK), .Q(reg1bit_8_q));
  reg1bit reg1bit_9 (.D(reg1bit_8_q), .WE(WE), .CK(CK), .Q(reg1bit_9_q));
  reg1bit reg1bit_10 (.D(reg1bit_9_q), .WE(WE), .CK(CK), .Q(A5B5));
  reg1bit reg1bit_11 (.D(A[0]), .WE(WE), .CK(CK), .Q(reg1bit_11_q));
  reg1bit reg1bit_12 (.D(A[1]), .WE(WE), .CK(CK), .Q(reg1bit_12_q));
  reg1bit reg1bit_13 (.D(A[2]), .WE(WE), .CK(CK), .Q(reg1bit_13_q));
  reg1bit reg1bit_14 (.D(A[3]), .WE(WE), .CK(CK), .Q(reg1bit_14_q));
  reg1bit reg1bit_15 (.D(A[4]), .WE(WE), .CK(CK), .Q(reg1bit_15_q));
  reg1bit reg1bit_16 (.D(A[5]), .WE(WE), .CK(CK), .Q(reg1bit_16_q));
  reg1bit reg1bit_17 (.D(B[0]), .WE(WE), .CK(CK), .Q(reg1bit_17_q));
  reg1bit reg1bit_18 (.D(B[1]), .WE(WE), .CK(CK), .Q(reg1bit_18_q));
  reg1bit reg1bit_19 (.D(B[2]), .WE(WE), .CK(CK), .Q(reg1bit_19_q));
  reg1bit reg1bit_20 (.D(B[3]), .WE(WE), .CK(CK), .Q(reg1bit_20_q));
  reg1bit reg1bit_21 (.D(B[4]), .WE(WE), .CK(CK), .Q(reg1bit_21_q));
  reg1bit reg1bit_22 (.D(B[5]), .WE(WE), .CK(CK), .Q(reg1bit_22_q));
  and and_5 (and_5_out, B[2], A[4]);
  reg1bit reg1bit_23 (.D(and_5_out), .WE(WE), .CK(CK), .Q(A4B2));
  and and_6 (and_6_out, B[3], A[4]);
  reg1bit reg1bit_24 (.D(and_6_out), .WE(WE), .CK(CK), .Q(reg1bit_24_q));
  reg1bit reg1bit_25 (.D(reg1bit_24_q), .WE(WE), .CK(CK), .Q(A4B3));
  and and_7 (and_7_out, B[4], A[4]);
  reg1bit reg1bit_26 (.D(and_7_out), .WE(WE), .CK(CK), .Q(reg1bit_26_q));
  reg1bit reg1bit_27 (.D(reg1bit_26_q), .WE(WE), .CK(CK), .Q(reg1bit_27_q));
  reg1bit reg1bit_28 (.D(reg1bit_27_q), .WE(WE), .CK(CK), .Q(A4B4));
  and and_8 (and_8_out, B[5], A[4]);
  reg1bit reg1bit_29 (.D(and_8_out), .WE(WE), .CK(CK), .Q(reg1bit_29_q));
  reg1bit reg1bit_30 (.D(reg1bit_29_q), .WE(WE), .CK(CK), .Q(reg1bit_30_q));
  reg1bit reg1bit_31 (.D(reg1bit_30_q), .WE(WE), .CK(CK), .Q(reg1bit_31_q));
  reg1bit reg1bit_32 (.D(reg1bit_31_q), .WE(WE), .CK(CK), .Q(A4B5));
  reg1bit reg1bit_33 (.D(reg1bit_11_q), .WE(WE), .CK(CK), .Q(reg1bit_33_q));
  reg1bit reg1bit_34 (.D(reg1bit_12_q), .WE(WE), .CK(CK), .Q(reg1bit_34_q));
  reg1bit reg1bit_35 (.D(reg1bit_13_q), .WE(WE), .CK(CK), .Q(reg1bit_35_q));
  reg1bit reg1bit_36 (.D(reg1bit_14_q), .WE(WE), .CK(CK), .Q(reg1bit_36_q));
  reg1bit reg1bit_37 (.D(reg1bit_15_q), .WE(WE), .CK(CK), .Q(reg1bit_37_q));
  reg1bit reg1bit_38 (.D(reg1bit_16_q), .WE(WE), .CK(CK), .Q(reg1bit_38_q));
  reg1bit reg1bit_39 (.D(reg1bit_17_q), .WE(WE), .CK(CK), .Q(reg1bit_39_q));
  reg1bit reg1bit_40 (.D(reg1bit_18_q), .WE(WE), .CK(CK), .Q(reg1bit_40_q));
  reg1bit reg1bit_41 (.D(reg1bit_19_q), .WE(WE), .CK(CK), .Q(reg1bit_41_q));
  reg1bit reg1bit_42 (.D(reg1bit_20_q), .WE(WE), .CK(CK), .Q(reg1bit_42_q));
  reg1bit reg1bit_43 (.D(reg1bit_21_q), .WE(WE), .CK(CK), .Q(reg1bit_43_q));
  reg1bit reg1bit_44 (.D(reg1bit_22_q), .WE(WE), .CK(CK), .Q(reg1bit_44_q));
  reg1bit reg1bit_45 (.D(reg1bit_33_q), .WE(WE), .CK(CK), .Q(reg1bit_45_q));
  reg1bit reg1bit_46 (.D(reg1bit_34_q), .WE(WE), .CK(CK), .Q(reg1bit_46_q));
  reg1bit reg1bit_47 (.D(reg1bit_35_q), .WE(WE), .CK(CK), .Q(reg1bit_47_q));
  reg1bit reg1bit_48 (.D(reg1bit_36_q), .WE(WE), .CK(CK), .Q(reg1bit_48_q));
  reg1bit reg1bit_49 (.D(reg1bit_37_q), .WE(WE), .CK(CK), .Q(reg1bit_49_q));
  reg1bit reg1bit_50 (.D(reg1bit_38_q), .WE(WE), .CK(CK), .Q(reg1bit_50_q));
  reg1bit reg1bit_51 (.D(reg1bit_39_q), .WE(WE), .CK(CK), .Q(reg1bit_51_q));
  reg1bit reg1bit_52 (.D(reg1bit_40_q), .WE(WE), .CK(CK), .Q(reg1bit_52_q));
  reg1bit reg1bit_53 (.D(reg1bit_41_q), .WE(WE), .CK(CK), .Q(reg1bit_53_q));
  reg1bit reg1bit_54 (.D(reg1bit_42_q), .WE(WE), .CK(CK), .Q(reg1bit_54_q));
  reg1bit reg1bit_55 (.D(reg1bit_43_q), .WE(WE), .CK(CK), .Q(reg1bit_55_q));
  reg1bit reg1bit_56 (.D(reg1bit_44_q), .WE(WE), .CK(CK), .Q(reg1bit_56_q));
  and and_9 (and_9_out, B[2], A[3]);
  reg1bit reg1bit_57 (.D(and_9_out), .WE(WE), .CK(CK), .Q(A3B2));
  and and_10 (and_10_out, B[3], A[3]);
  reg1bit reg1bit_58 (.D(and_10_out), .WE(WE), .CK(CK), .Q(reg1bit_58_q));
  reg1bit reg1bit_59 (.D(reg1bit_58_q), .WE(WE), .CK(CK), .Q(A3B3));
  and and_11 (and_11_out, B[4], A[3]);
  reg1bit reg1bit_60 (.D(and_11_out), .WE(WE), .CK(CK), .Q(reg1bit_60_q));
  reg1bit reg1bit_61 (.D(reg1bit_60_q), .WE(WE), .CK(CK), .Q(reg1bit_61_q));
  reg1bit reg1bit_62 (.D(reg1bit_61_q), .WE(WE), .CK(CK), .Q(A3B4));
  and and_12 (and_12_out, B[5], A[3]);
  reg1bit reg1bit_63 (.D(and_12_out), .WE(WE), .CK(CK), .Q(reg1bit_63_q));
  reg1bit reg1bit_64 (.D(reg1bit_63_q), .WE(WE), .CK(CK), .Q(reg1bit_64_q));
  reg1bit reg1bit_65 (.D(reg1bit_64_q), .WE(WE), .CK(CK), .Q(reg1bit_65_q));
  reg1bit reg1bit_66 (.D(reg1bit_65_q), .WE(WE), .CK(CK), .Q(A3B5));
  reg1bit reg1bit_67 (.D(reg1bit_45_q), .WE(WE), .CK(CK), .Q(reg1bit_67_q));
  reg1bit reg1bit_68 (.D(reg1bit_46_q), .WE(WE), .CK(CK), .Q(reg1bit_68_q));
  reg1bit reg1bit_69 (.D(reg1bit_47_q), .WE(WE), .CK(CK), .Q(reg1bit_69_q));
  reg1bit reg1bit_70 (.D(reg1bit_48_q), .WE(WE), .CK(CK), .Q(reg1bit_70_q));
  reg1bit reg1bit_71 (.D(reg1bit_49_q), .WE(WE), .CK(CK), .Q(reg1bit_71_q));
  reg1bit reg1bit_72 (.D(reg1bit_50_q), .WE(WE), .CK(CK), .Q(reg1bit_72_q));
  reg1bit reg1bit_73 (.D(reg1bit_51_q), .WE(WE), .CK(CK), .Q(reg1bit_73_q));
  reg1bit reg1bit_74 (.D(reg1bit_52_q), .WE(WE), .CK(CK), .Q(reg1bit_74_q));
  reg1bit reg1bit_75 (.D(reg1bit_53_q), .WE(WE), .CK(CK), .Q(reg1bit_75_q));
  reg1bit reg1bit_76 (.D(reg1bit_54_q), .WE(WE), .CK(CK), .Q(reg1bit_76_q));
  reg1bit reg1bit_77 (.D(reg1bit_55_q), .WE(WE), .CK(CK), .Q(reg1bit_77_q));
  reg1bit reg1bit_78 (.D(reg1bit_56_q), .WE(WE), .CK(CK), .Q(reg1bit_78_q));
  and and_13 (and_13_out, B[2], A[2]);
  reg1bit reg1bit_79 (.D(and_13_out), .WE(WE), .CK(CK), .Q(A2B2));
  and and_14 (and_14_out, B[3], A[2]);
  reg1bit reg1bit_80 (.D(and_14_out), .WE(WE), .CK(CK), .Q(reg1bit_80_q));
  reg1bit reg1bit_81 (.D(reg1bit_80_q), .WE(WE), .CK(CK), .Q(A2B3));
  and and_15 (and_15_out, B[4], A[2]);
  reg1bit reg1bit_82 (.D(and_15_out), .WE(WE), .CK(CK), .Q(reg1bit_82_q));
  reg1bit reg1bit_83 (.D(reg1bit_82_q), .WE(WE), .CK(CK), .Q(reg1bit_83_q));
  reg1bit reg1bit_84 (.D(reg1bit_83_q), .WE(WE), .CK(CK), .Q(A2B4));
  and and_16 (and_16_out, B[5], A[2]);
  reg1bit reg1bit_85 (.D(and_16_out), .WE(WE), .CK(CK), .Q(reg1bit_85_q));
  reg1bit reg1bit_86 (.D(reg1bit_85_q), .WE(WE), .CK(CK), .Q(reg1bit_86_q));
  reg1bit reg1bit_87 (.D(reg1bit_86_q), .WE(WE), .CK(CK), .Q(reg1bit_87_q));
  reg1bit reg1bit_88 (.D(reg1bit_87_q), .WE(WE), .CK(CK), .Q(A2B5));
  reg1bit reg1bit_89 (.D(reg1bit_67_q), .WE(WE), .CK(CK), .Q(AO[0]));
  reg1bit reg1bit_90 (.D(reg1bit_68_q), .WE(WE), .CK(CK), .Q(AO[1]));
  reg1bit reg1bit_91 (.D(reg1bit_69_q), .WE(WE), .CK(CK), .Q(AO[2]));
  reg1bit reg1bit_92 (.D(reg1bit_70_q), .WE(WE), .CK(CK), .Q(AO[3]));
  reg1bit reg1bit_93 (.D(reg1bit_71_q), .WE(WE), .CK(CK), .Q(AO[4]));
  reg1bit reg1bit_94 (.D(reg1bit_72_q), .WE(WE), .CK(CK), .Q(AO[5]));
  reg1bit reg1bit_95 (.D(reg1bit_73_q), .WE(WE), .CK(CK), .Q(BO[0]));
  reg1bit reg1bit_96 (.D(reg1bit_74_q), .WE(WE), .CK(CK), .Q(BO[1]));
  reg1bit reg1bit_97 (.D(reg1bit_75_q), .WE(WE), .CK(CK), .Q(BO[2]));
  reg1bit reg1bit_98 (.D(reg1bit_76_q), .WE(WE), .CK(CK), .Q(BO[3]));
  reg1bit reg1bit_99 (.D(reg1bit_77_q), .WE(WE), .CK(CK), .Q(BO[4]));
  reg1bit reg1bit_100 (.D(reg1bit_78_q), .WE(WE), .CK(CK), .Q(BO[5]));
  and and_17 (and_17_out, B[2], A[1]);
  reg1bit reg1bit_101 (.D(and_17_out), .WE(WE), .CK(CK), .Q(A1B2));
  and and_18 (and_18_out, B[3], A[1]);
  reg1bit reg1bit_102 (.D(and_18_out), .WE(WE), .CK(CK), .Q(reg1bit_102_q));
  reg1bit reg1bit_103 (.D(reg1bit_102_q), .WE(WE), .CK(CK), .Q(A1B3));
  and and_19 (and_19_out, B[4], A[1]);
  reg1bit reg1bit_104 (.D(and_19_out), .WE(WE), .CK(CK), .Q(reg1bit_104_q));
  reg1bit reg1bit_105 (.D(reg1bit_104_q), .WE(WE), .CK(CK), .Q(reg1bit_105_q));
  reg1bit reg1bit_106 (.D(reg1bit_105_q), .WE(WE), .CK(CK), .Q(A1B4));
  and and_20 (and_20_out, B[5], A[1]);
  reg1bit reg1bit_107 (.D(and_20_out), .WE(WE), .CK(CK), .Q(reg1bit_107_q));
  reg1bit reg1bit_108 (.D(reg1bit_107_q), .WE(WE), .CK(CK), .Q(reg1bit_108_q));
  reg1bit reg1bit_109 (.D(reg1bit_108_q), .WE(WE), .CK(CK), .Q(reg1bit_109_q));
  reg1bit reg1bit_110 (.D(reg1bit_109_q), .WE(WE), .CK(CK), .Q(A1B5));
  reg1bit reg1bit_111 (.D(fa_1_cout), .WE(WE), .CK(CK), .Q(P[11]));
  and and_21 (and_21_out, B[2], A[0]);
  reg1bit reg1bit_112 (.D(and_21_out), .WE(WE), .CK(CK), .Q(A0B2));
  and and_22 (and_22_out, B[3], A[0]);
  reg1bit reg1bit_113 (.D(and_22_out), .WE(WE), .CK(CK), .Q(reg1bit_113_q));
  reg1bit reg1bit_114 (.D(reg1bit_113_q), .WE(WE), .CK(CK), .Q(A0B3));
  and and_23 (and_23_out, B[4], A[0]);
  reg1bit reg1bit_115 (.D(and_23_out), .WE(WE), .CK(CK), .Q(reg1bit_115_q));
  reg1bit reg1bit_116 (.D(reg1bit_115_q), .WE(WE), .CK(CK), .Q(reg1bit_116_q));
  reg1bit reg1bit_117 (.D(reg1bit_116_q), .WE(WE), .CK(CK), .Q(A0B4));
  and and_24 (and_24_out, B[5], A[0]);
  reg1bit reg1bit_118 (.D(and_24_out), .WE(WE), .CK(CK), .Q(reg1bit_118_q));
  reg1bit reg1bit_119 (.D(reg1bit_118_q), .WE(WE), .CK(CK), .Q(reg1bit_119_q));
  reg1bit reg1bit_120 (.D(reg1bit_119_q), .WE(WE), .CK(CK), .Q(reg1bit_120_q));
  reg1bit reg1bit_121 (.D(reg1bit_120_q), .WE(WE), .CK(CK), .Q(A0B5));
  reg1bit reg1bit_122 (.D(fa_2_cout), .WE(WE), .CK(CK), .Q(reg1bit_122_q));
  reg1bit reg1bit_123 (.D(fa_1_sum), .WE(WE), .CK(CK), .Q(P[10]));
  reg1bit reg1bit_124 (.D(fa_4_cout), .WE(WE), .CK(CK), .Q(reg1bit_124_q));
  FA fa_1 (.A(A5B5), .B(reg1bit_122_q), .Cin(fa_3_cout), .Cout(fa_1_cout), .Sum(fa_1_sum));
  FA fa_2 (.A(A5B4), .B(reg1bit_124_q), .Cin(fa_6_cout), .Cout(fa_2_cout), .Sum(fa_2_sum));
  reg1bit reg1bit_125 (.D(fa_2_sum), .WE(WE), .CK(CK), .Q(reg1bit_125_q));
  FA fa_3 (.A(A4B5), .B(reg1bit_125_q), .Cin(fa_7_cout), .Cout(fa_3_cout), .Sum(fa_3_sum));
  reg1bit reg1bit_126 (.D(fa_3_sum), .WE(WE), .CK(CK), .Q(P[9]));
  reg1bit reg1bit_127 (.D(fa_5_cout), .WE(WE), .CK(CK), .Q(reg1bit_127_q));
  FA fa_4 (.A(A5B3), .B(reg1bit_127_q), .Cin(fa_8_cout), .Cout(fa_4_cout), .Sum(fa_4_sum));
  reg1bit reg1bit_128 (.D(fa_4_sum), .WE(WE), .CK(CK), .Q(reg1bit_128_q));
  reg1bit reg1bit_129 (.D(fa_6_sum), .WE(WE), .CK(CK), .Q(reg1bit_129_q));
  reg1bit reg1bit_130 (.D(ha_1_cout), .WE(WE), .CK(CK), .Q(reg1bit_130_q));
  FA fa_5 (.A(A5B2), .B(reg1bit_130_q), .Cin(fa_10_cout), .Cout(fa_5_cout), .Sum(fa_5_sum));
  reg1bit reg1bit_131 (.D(fa_5_sum), .WE(WE), .CK(CK), .Q(reg1bit_131_q));
  FA fa_6 (.A(A4B4), .B(reg1bit_128_q), .Cin(fa_9_cout), .Cout(fa_6_cout), .Sum(fa_6_sum));
  FA fa_7 (.A(A3B5), .B(reg1bit_129_q), .Cin(fa_12_cout), .Cout(fa_7_cout), .Sum(fa_7_sum));
  reg1bit reg1bit_132 (.D(fa_7_sum), .WE(WE), .CK(CK), .Q(P[8]));
  reg1bit reg1bit_133 (.D(ha_1_s), .WE(WE), .CK(CK), .Q(reg1bit_133_q));
  FA fa_8 (.A(A4B3), .B(reg1bit_131_q), .Cin(fa_11_cout), .Cout(fa_8_cout), .Sum(fa_8_sum));
  reg1bit reg1bit_134 (.D(fa_8_sum), .WE(WE), .CK(CK), .Q(reg1bit_134_q));
  FA fa_9 (.A(A3B4), .B(reg1bit_134_q), .Cin(fa_14_cout), .Cout(fa_9_cout), .Sum(fa_9_sum));
  reg1bit reg1bit_135 (.D(fa_9_sum), .WE(WE), .CK(CK), .Q(reg1bit_135_q));
  reg1bit reg1bit_136 (.D(fa_12_sum), .WE(WE), .CK(CK), .Q(P[7]));
  and and_25 (and_25_out, B[1], A[5]);
  HA ha_1 (.A(and_25_out), .B(fa_13_cout), .Cout(ha_1_cout), .S(ha_1_s));
  FA fa_10 (.A(A4B2), .B(reg1bit_133_q), .Cin(fa_16_cout), .Cout(fa_10_cout), .Sum(fa_10_sum));
  reg1bit reg1bit_137 (.D(fa_10_sum), .WE(WE), .CK(CK), .Q(reg1bit_137_q));
  FA fa_11 (.A(A3B3), .B(reg1bit_137_q), .Cin(fa_17_cout), .Cout(fa_11_cout), .Sum(fa_11_sum));
  reg1bit reg1bit_138 (.D(fa_11_sum), .WE(WE), .CK(CK), .Q(reg1bit_138_q));
  FA fa_12 (.A(A2B5), .B(reg1bit_135_q), .Cin(fa_15_cout), .Cout(fa_12_cout), .Sum(fa_12_sum));
  and and_26 (and_26_out, B[0], A[5]);
  and and_27 (and_27_out, B[1], A[4]);
  FA fa_13 (.A(and_27_out), .B(and_26_out), .Cin(fa_19_cout), .Cout(fa_13_cout), .Sum(fa_13_sum));
  reg1bit reg1bit_139 (.D(fa_13_sum), .WE(WE), .CK(CK), .Q(reg1bit_139_q));
  reg1bit reg1bit_140 (.D(fa_16_sum), .WE(WE), .CK(CK), .Q(reg1bit_140_q));
  FA fa_14 (.A(A2B4), .B(reg1bit_138_q), .Cin(fa_18_cout), .Cout(fa_14_cout), .Sum(fa_14_sum));
  reg1bit reg1bit_141 (.D(fa_14_sum), .WE(WE), .CK(CK), .Q(reg1bit_141_q));
  FA fa_15 (.A(A1B5), .B(reg1bit_141_q), .Cin(ha_2_cout), .Cout(fa_15_cout), .Sum(fa_15_sum));
  reg1bit reg1bit_142 (.D(fa_15_sum), .WE(WE), .CK(CK), .Q(P[6]));
  and and_28 (and_28_out, B[0], A[4]);
  FA fa_16 (.A(A3B2), .B(reg1bit_139_q), .Cin(fa_20_cout), .Cout(fa_16_cout), .Sum(fa_16_sum));
  FA fa_17 (.A(A2B3), .B(reg1bit_140_q), .Cin(fa_21_cout), .Cout(fa_17_cout), .Sum(fa_17_sum));
  reg1bit reg1bit_143 (.D(fa_17_sum), .WE(WE), .CK(CK), .Q(reg1bit_143_q));
  FA fa_18 (.A(A1B4), .B(reg1bit_143_q), .Cin(ha_3_cout), .Cout(fa_18_cout), .Sum(fa_18_sum));
  reg1bit reg1bit_144 (.D(fa_18_sum), .WE(WE), .CK(CK), .Q(reg1bit_144_q));
  and and_29 (and_29_out, B[1], A[3]);
  FA fa_19 (.A(and_29_out), .B(and_28_out), .Cin(fa_22_cout), .Cout(fa_19_cout), .Sum(fa_19_sum));
  reg1bit reg1bit_145 (.D(fa_19_sum), .WE(WE), .CK(CK), .Q(reg1bit_145_q));
  FA fa_20 (.A(A2B2), .B(reg1bit_145_q), .Cin(fa_23_cout), .Cout(fa_20_cout), .Sum(fa_20_sum));
  reg1bit reg1bit_146 (.D(fa_20_sum), .WE(WE), .CK(CK), .Q(reg1bit_146_q));
  reg1bit reg1bit_147 (.D(fa_21_sum), .WE(WE), .CK(CK), .Q(reg1bit_147_q));
  HA ha_2 (.A(A0B5), .B(reg1bit_144_q), .Cout(ha_2_cout), .S(ha_2_s));
  reg1bit reg1bit_148 (.D(ha_2_s), .WE(WE), .CK(CK), .Q(P[5]));
  and and_30 (and_30_out, B[0], A[3]);
  reg1bit reg1bit_149 (.D(fa_22_sum), .WE(WE), .CK(CK), .Q(reg1bit_149_q));
  FA fa_21 (.A(A1B3), .B(reg1bit_146_q), .Cin(ha_4_cout), .Cout(fa_21_cout), .Sum(fa_21_sum));
  HA ha_3 (.A(A0B4), .B(reg1bit_147_q), .Cout(ha_3_cout), .S(ha_3_s));
  reg1bit reg1bit_150 (.D(ha_3_s), .WE(WE), .CK(CK), .Q(reg1bit_150_q));
  and and_31 (and_31_out, B[1], A[2]);
  FA fa_22 (.A(and_31_out), .B(and_30_out), .Cin(fa_24_cout), .Cout(fa_22_cout), .Sum(fa_22_sum));
  FA fa_23 (.A(A1B2), .B(reg1bit_149_q), .Cin(ha_5_cout), .Cout(fa_23_cout), .Sum(fa_23_sum));
  reg1bit reg1bit_151 (.D(fa_23_sum), .WE(WE), .CK(CK), .Q(reg1bit_151_q));
  HA ha_4 (.A(A0B3), .B(reg1bit_151_q), .Cout(ha_4_cout), .S(ha_4_s));
  reg1bit reg1bit_152 (.D(ha_4_s), .WE(WE), .CK(CK), .Q(reg1bit_152_q));
  and and_32 (and_32_out, B[0], A[2]);
  and and_33 (and_33_out, B[1], A[1]);
  FA fa_24 (.A(and_33_out), .B(and_32_out), .Cin(ha_6_cout), .Cout(fa_24_cout), .Sum(fa_24_sum));
  reg1bit reg1bit_153 (.D(fa_24_sum), .WE(WE), .CK(CK), .Q(reg1bit_153_q));
  reg1bit reg1bit_154 (.D(ha_5_s), .WE(WE), .CK(CK), .Q(reg1bit_154_q));
  reg1bit reg1bit_155 (.D(reg1bit_150_q), .WE(WE), .CK(CK), .Q(P[4]));
  and and_34 (and_34_out, B[0], A[1]);
  HA ha_5 (.A(A0B2), .B(reg1bit_153_q), .Cout(ha_5_cout), .S(ha_5_s));
  reg1bit reg1bit_156 (.D(reg1bit_152_q), .WE(WE), .CK(CK), .Q(reg1bit_156_q));
  and and_35 (and_35_out, B[1], A[0]);
  HA ha_6 (.A(and_35_out), .B(and_34_out), .Cout(ha_6_cout), .S(ha_6_s));
  reg1bit reg1bit_157 (.D(ha_6_s), .WE(WE), .CK(CK), .Q(reg1bit_157_q));
  reg1bit reg1bit_158 (.D(reg1bit_154_q), .WE(WE), .CK(CK), .Q(reg1bit_158_q));
  and and_36 (and_36_out, B[0], A[0]);
  reg1bit reg1bit_159 (.D(reg1bit_156_q), .WE(WE), .CK(CK), .Q(P[3]));
  reg1bit reg1bit_160 (.D(reg1bit_157_q), .WE(WE), .CK(CK), .Q(reg1bit_160_q));
  reg1bit reg1bit_161 (.D(reg1bit_158_q), .WE(WE), .CK(CK), .Q(reg1bit_161_q));
  reg1bit reg1bit_162 (.D(and_36_out), .WE(WE), .CK(CK), .Q(reg1bit_162_q));
  reg1bit reg1bit_163 (.D(reg1bit_160_q), .WE(WE), .CK(CK), .Q(reg1bit_163_q));
  reg1bit reg1bit_164 (.D(reg1bit_161_q), .WE(WE), .CK(CK), .Q(P[2]));
  reg1bit reg1bit_165 (.D(reg1bit_162_q), .WE(WE), .CK(CK), .Q(reg1bit_165_q));
  reg1bit reg1bit_166 (.D(reg1bit_163_q), .WE(WE), .CK(CK), .Q(reg1bit_166_q));
  reg1bit reg1bit_167 (.D(reg1bit_165_q), .WE(WE), .CK(CK), .Q(reg1bit_167_q));
  reg1bit reg1bit_168 (.D(reg1bit_166_q), .WE(WE), .CK(CK), .Q(P[1]));
  reg1bit reg1bit_169 (.D(reg1bit_167_q), .WE(WE), .CK(CK), .Q(reg1bit_169_q));
  reg1bit reg1bit_170 (.D(reg1bit_169_q), .WE(WE), .CK(CK), .Q(P[0]));

  // Notes on the sheet:
  //   Attention, votre version de Logisim
  //   ne contient pas de tracker. Si vous
  //   enregistrez votre projet, toutes les
  //   informations du tracker seront
  //   définitivement effacées.
endmodule

module HA (
  input  A,
  input  B,
  output Cout,
  output S
);

  and and_1 (Cout, A, B);
  xor xor_1 (S, A, B);

  // Notes on the sheet:
  //   Attention, votre version de Logisim
  //   ne contient pas de tracker. Si vous
  //   enregistrez votre projet, toutes les
  //   informations du tracker seront
  //   définitivement effacées.
endmodule

module FA (
  input  A,
  input  B,
  input  Cin,
  output Cout,
  output Sum
);

  wire and_1_out, and_2_out, xor_1_out;

  and and_1 (and_1_out, A, B);
  and and_2 (and_2_out, xor_1_out, Cin);
  or or_1 (Cout, and_1_out, and_2_out);
  xor xor_1 (xor_1_out, A, B);
  xor xor_2 (Sum, xor_1_out, Cin);

  // Notes on the sheet:
  //   Attention, votre version de Logisim
  //   ne contient pas de tracker. Si vous
  //   enregistrez votre projet, toutes les
  //   informations du tracker seront
  //   définitivement effacées.
endmodule

module reg1bit (
  input  D,
  input  WE,
  input  CK,
  output Q
);

  Register #(.width(1)) register_1 (.D(D), .en(WE), .clk(CK), .Q(Q));  // open: clr

  // Notes on the sheet:
  //   Attention, votre version de Logisim
  //   ne contient pas de tracker. Si vous
  //   enregistrez votre projet, toutes les
  //   informations du tracker seront
  //   définitivement effacées.
endmodule
