// Logisim project 6-bit_Pipelined_Parallel_Unsigned_Binary_Divider.circ as structural Verilog: 4 circuits, main circuit main
module main (
  output halt,
  output [5:0] N,
  output [5:0] D,
  output [5:0] Q,
  output [5:0] R
);

  wire and_1_out, clock_1_out, comparator_1_eq, comparator_2_eq, comparator_3_eq, d_ff_1_q, d_ff_2_q,
       or_1_out;
  wire [5:0] divider_1_out, divider_1_rem;
  wire [11:0] random_1_out;

  Counter #(.width(12), .max('hfff)) counter_1 (.clk(clock_1_out), .carry(halt));  // open: clr, load, up, count, D, Q
  Clock clock_1 (.out(clock_1_out));
  Random #(.width(12)) random_1 (.next(or_1_out), .clk(clock_1_out), .out(random_1_out));  // open: clr
  // Probe on random_1_out[5:0]
  // Probe on random_1_out[11:6]
  RAM #(.addrWidth(12), .dataWidth(1), .trigger("falling"), .databus("bibus")) ram_1 (
    .addr(random_1_out), .we(or_1_out), .clk(clock_1_out));  // open: oe, din, dout
  mycircuit mycircuit_1 (
    .N(random_1_out[5:0]), .D(random_1_out[11:6]), .CK(clock_1_out), .WE(or_1_out), .NO(N), .DO(D), .Q(Q),
    .R(R));
  // Probe on N
  // Probe on D
  Divider #(.width(6)) divider_1 (.a(N), .b(D), .out(divider_1_out), .rem(divider_1_rem));  // open: upper
  // Probe on Q
  Comparator #(.width(6)) comparator_1 (.a(Q), .b(divider_1_out), .eq(comparator_1_eq));  // open: gt, lt
  // Probe on divider_1_out
  // Probe on divider_1_rem
  Comparator #(.width(6)) comparator_2 (.a(divider_1_rem), .b(R), .eq(comparator_2_eq));  // open: gt, lt
  // Probe on R
  D_Flip_Flop #(.trigger("falling")) d_ff_1 (
    .D(comparator_1_eq), .clk(clock_1_out), .Q(d_ff_1_q));  // open: Qn, preset, reset
  D_Flip_Flop #(.trigger("falling")) d_ff_2 (
    .D(comparator_2_eq), .clk(clock_1_out), .Q(d_ff_2_q));  // open: Qn, preset, reset
  or or_1 (or_1_out, comparator_3_eq, and_1_out);
  and and_1 (and_1_out, d_ff_1_q, d_ff_2_q);
  Comparator #(.width(6)) comparator_3 (.a(D), .b({6{1'b0}}), .eq(comparator_3_eq));  // open: gt, lt

  // Notes on the sheet:
  //   Attention, votre version de Logisim
  //   ne contient pas de tracker. Si vous
  //   enregistrez votre projet, toutes les
  //   informations du tracker seront
  //   définitivement effacées.
endmodule

module mycircuit (
  input  [5:0] N,
  input  [5:0] D,
  input  CK,
  input  WE,
  output [5:0] NO,
  output [5:0] DO,
  output [5:0] Q,
  output [5:0] R
);

  wire A0f, A1e, A2d, A3c, A4b, A5a, B0a, B0b, B0c, B0d, B0e, B0f, B1a, B1b, B1c, B1d, B1e, B1f, B2a, B2b,
       B2c, B2d, B2e, B2f, B3a, B3b, B3c, B3d, B3e, B3f, B4a, B4b, B4c, B4d, B4e, B4f, B5a, B5b, B5c, B5d,
       B5e, B5f, pu_1_cout, pu_2_cout, pu_2_r, pu_3_cout, pu_4_cout, pu_4_r, pu_5_cout, pu_5_r, pu_6_cout,
       pu_7_cout, pu_7_r, pu_8_cout, pu_8_r, pu_9_cout, pu_9_r, pu_10_cout, pu_11_cout, pu_11_r, pu_12_cout,
       pu_12_r, pu_13_cout, pu_13_r, pu_14_cout, pu_14_r, pu_15_cout, pu_16_cout, pu_16_r, pu_17_cout,
       pu_17_r, pu_18_cout, pu_18_r, pu_19_cout, pu_19_r, pu_20_cout, pu_20_r, pu_22_cout, pu_23_cout,
       pu_23_r, pu_24_cout, pu_24_r, pu_25_cout, pu_25_r, pu_26_cout, pu_26_r, pu_27_cout, pu_27_r,
       pu_28_cout, pu_28_r, pu_29_cout, pu_29_r, pu_30_cout, pu_31_cout, pu_31_r, pu_32_cout, pu_32_r,
       pu_33_cout, pu_34_cout, pu_34_r, pu_35_cout, pu_36_cout, reg1bit_1_q, reg1bit_2_q, reg1bit_3_q,
       reg1bit_4_q, reg1bit_5_q, reg1bit_6_q, reg1bit_7_q, reg1bit_8_q, reg1bit_9_q, reg1bit_10_q,
       reg1bit_11_q, reg1bit_12_q, reg1bit_13_q, reg1bit_14_q, reg1bit_15_q, reg1bit_16_q, reg1bit_17_q,
       reg1bit_18_q, reg1bit_19_q, reg1bit_20_q, reg1bit_21_q, reg1bit_22_q, reg1bit_23_q, reg1bit_24_q,
       reg1bit_25_q, reg1bit_26_q, reg1bit_27_q, reg1bit_28_q, reg1bit_30_q, reg1bit_31_q, reg1bit_32_q,
       reg1bit_33_q, reg1bit_34_q, reg1bit_37_q, reg1bit_38_q, reg1bit_42_q, reg1bit_43_q, reg1bit_44_q,
       reg1bit_45_q, reg1bit_46_q, reg1bit_54_q, reg1bit_55_q, reg1bit_56_q, reg1bit_57_q, reg1bit_65_q,
       reg1bit_66_q, reg1bit_67_q, reg1bit_75_q, reg1bit_76_q, reg1bit_84_q;
  wire [5:0] register_1_q, register_2_q, register_3_q, register_4_q, register_5_q, register_7_q,
       register_8_q, register_9_q, register_10_q, register_11_q;

  Register #(.width(6)) register_1 (.D(N), .en(WE), .clk(CK), .Q(register_1_q));  // open: clr
  Register #(.width(6)) register_2 (.D(register_1_q), .en(WE), .clk(CK), .Q(register_2_q));  // open: clr
  PU pu_1 (.A(1'b0), .B(B5a), .Cin(pu_2_cout), .S(pu_1_cout), .Cout(pu_1_cout));  // open: R
  Register #(.width(6)) register_3 (.D(register_2_q), .en(WE), .clk(CK), .Q(register_3_q));  // open: clr
  Register #(.width(6)) register_4 (.D(register_3_q), .en(WE), .clk(CK), .Q(register_4_q));  // open: clr
  PU pu_2 (.A(1'b0), .B(B4a), .Cin(pu_4_cout), .S(pu_1_cout), .R(pu_2_r), .Cout(pu_2_cout));
  PU pu_3 (.A(reg1bit_1_q), .B(B5b), .Cin(pu_5_cout), .S(pu_3_cout), .Cout(pu_3_cout));  // open: R
  Register #(.width(6)) register_5 (.D(register_4_q), .en(WE), .clk(CK), .Q(register_5_q));  // open: clr
  reg1bit reg1bit_1 (.D(pu_2_r), .WE(WE), .CK(CK), .Q(reg1bit_1_q));
  Register #(.width(6)) register_6 (.D(register_5_q), .en(WE), .clk(CK), .Q(NO));  // open: clr
  PU pu_4 (.A(1'b0), .B(B3a), .Cin(pu_7_cout), .S(pu_1_cout), .R(pu_4_r), .Cout(pu_4_cout));
  reg1bit reg1bit_2 (.D(pu_4_r), .WE(WE), .CK(CK), .Q(reg1bit_2_q));
  PU pu_5 (.A(reg1bit_2_q), .B(B4b), .Cin(pu_8_cout), .S(pu_3_cout), .R(pu_5_r), .Cout(pu_5_cout));
  reg1bit reg1bit_3 (.D(pu_5_r), .WE(WE), .CK(CK), .Q(reg1bit_3_q));
  PU pu_6 (.A(reg1bit_3_q), .B(B5c), .Cin(pu_9_cout), .S(pu_6_cout), .Cout(pu_6_cout));  // open: R
  Register #(.width(6)) register_7 (.D(D), .en(WE), .clk(CK), .Q(register_7_q));  // open: clr
  Register #(.width(6)) register_8 (.D(register_7_q), .en(WE), .clk(CK), .Q(register_8_q));  // open: clr
  PU pu_7 (.A(1'b0), .B(B2a), .Cin(pu_11_cout), .S(pu_1_cout), .R(pu_7_r), .Cout(pu_7_cout));
  reg1bit reg1bit_4 (.D(pu_7_r), .WE(WE), .CK(CK), .Q(reg1bit_4_q));
  PU pu_8 (.A(reg1bit_4_q), .B(B3b), .Cin(pu_12_cout), .S(pu_3_cout), .R(pu_8_r), .Cout(pu_8_cout));
  reg1bit reg1bit_5 (.D(pu_8_r), .WE(WE), .CK(CK), .Q(reg1bit_5_q));
  PU pu_9 (.A(reg1bit_5_q), .B(B4c), .Cin(pu_13_cout), .S(pu_6_cout), .R(pu_9_r), .Cout(pu_9_cout));
  reg1bit reg1bit_6 (.D(pu_9_r), .WE(WE), .CK(CK), .Q(reg1bit_6_q));
  PU pu_10 (.A(reg1bit_6_q), .B(B5d), .Cin(pu_14_cout), .S(pu_10_cout), .Cout(pu_10_cout));  // open: R
  Register #(.width(6)) register_9 (.D(register_8_q), .en(WE), .clk(CK), .Q(register_9_q));  // open: clr
  Register #(.width(6)) register_10 (.D(register_9_q), .en(WE), .clk(CK), .Q(register_10_q));  // open: clr
  PU pu_11 (.A(1'b0), .B(B1a), .Cin(pu_16_cout), .S(pu_1_cout), .R(pu_11_r), .Cout(pu_11_cout));
  reg1bit reg1bit_7 (.D(pu_11_r), .WE(WE), .CK(CK), .Q(reg1bit_7_q));
  PU pu_12 (.A(reg1bit_7_q), .B(B2b), .Cin(pu_17_cout), .S(pu_3_cout), .R(pu_12_r), .Cout(pu_12_cout));
  reg1bit reg1bit_8 (.D(pu_12_r), .WE(WE), .CK(CK), .Q(reg1bit_8_q));
  PU pu_13 (.A(reg1bit_8_q), .B(B3c), .Cin(pu_18_cout), .S(pu_6_cout), .R(pu_13_r), .Cout(pu_13_cout));
  reg1bit reg1bit_9 (.D(pu_13_r), .WE(WE), .CK(CK), .Q(reg1bit_9_q));
  PU pu_14 (.A(reg1bit_9_q), .B(B4d), .Cin(pu_19_cout), .S(pu_10_cout), .R(pu_14_r), .Cout(pu_14_cout));
  reg1bit reg1bit_10 (.D(pu_14_r), .WE(WE), .CK(CK), .Q(reg1bit_10_q));
  PU pu_15 (.A(reg1bit_10_q), .B(B5e), .Cin(pu_20_cout), .S(pu_15_cout), .Cout(pu_15_cout));  // open: R
  Register #(.width(6)) register_11 (.D(register_10_q), .en(WE), .clk(CK), .Q(register_11_q));  // open: clr
  Register #(.width(6)) register_12 (.D(register_11_q), .en(WE), .clk(CK), .Q(DO));  // open: clr
  PU pu_16 (.A(A5a), .B(B0a), .Cin(1'b1), .S(pu_1_cout), .R(pu_16_r), .Cout(pu_16_cout));
  reg1bit reg1bit_11 (.D(pu_16_r), .WE(WE), .CK(CK), .Q(reg1bit_11_q));
  PU pu_17 (.A(reg1bit_11_q), .B(B1b), .Cin(pu_23_cout), .S(pu_3_cout), .R(pu_17_r), .Cout(pu_17_cout));
  reg1bit reg1bit_12 (.D(pu_17_r), .WE(WE), .CK(CK), .Q(reg1bit_12_q));
  PU pu_18 (.A(reg1bit_12_q), .B(B2c), .Cin(pu_24_cout), .S(pu_6_cout), .R(pu_18_r), .Cout(pu_18_cout));
  reg1bit reg1bit_13 (.D(pu_18_r), .WE(WE), .CK(CK), .Q(reg1bit_13_q));
  PU pu_19 (.A(reg1bit_13_q), .B(B3d), .Cin(pu_25_cout), .S(pu_10_cout), .R(pu_19_r), .Cout(pu_19_cout));
  reg1bit reg1bit_14 (.D(pu_19_r), .WE(WE), .CK(CK), .Q(reg1bit_14_q));
  PU pu_20 (.A(reg1bit_14_q), .B(B4e), .Cin(pu_26_cout), .S(pu_15_cout), .R(pu_20_r), .Cout(pu_20_cout));
  reg1bit reg1bit_15 (.D(pu_20_r), .WE(WE), .CK(CK), .Q(reg1bit_15_q));
  PU pu_21 (.A(reg1bit_15_q), .B(B5f), .Cin(pu_22_cout), .S(Q[0]), .R(R[5]), .Cout(Q[0]));
  reg1bit reg1bit_16 (.D(pu_1_cout), .WE(WE), .CK(CK), .Q(reg1bit_16_q));
  PU pu_22 (.A(reg1bit_20_q), .B(B4f), .Cin(pu_30_cout), .S(Q[0]), .R(R[4]), .Cout(pu_22_cout));
  PU pu_23 (.A(A4b), .B(B0b), .Cin(1'b1), .S(pu_3_cout), .R(pu_23_r), .Cout(pu_23_cout));
  reg1bit reg1bit_17 (.D(pu_23_r), .WE(WE), .CK(CK), .Q(reg1bit_17_q));
  PU pu_24 (.A(reg1bit_17_q), .B(B1c), .Cin(pu_27_cout), .S(pu_6_cout), .R(pu_24_r), .Cout(pu_24_cout));
  reg1bit reg1bit_18 (.D(pu_24_r), .WE(WE), .CK(CK), .Q(reg1bit_18_q));
  PU pu_25 (.A(reg1bit_18_q), .B(B2d), .Cin(pu_28_cout), .S(pu_10_cout), .R(pu_25_r), .Cout(pu_25_cout));
  reg1bit reg1bit_19 (.D(pu_25_r), .WE(WE), .CK(CK), .Q(reg1bit_19_q));
  PU pu_26 (.A(reg1bit_19_q), .B(B3e), .Cin(pu_29_cout), .S(pu_15_cout), .R(pu_26_r), .Cout(pu_26_cout));
  reg1bit reg1bit_20 (.D(pu_26_r), .WE(WE), .CK(CK), .Q(reg1bit_20_q));
  reg1bit reg1bit_21 (.D(reg1bit_16_q), .WE(WE), .CK(CK), .Q(reg1bit_21_q));
  reg1bit reg1bit_22 (.D(reg1bit_21_q), .WE(WE), .CK(CK), .Q(reg1bit_22_q));
  reg1bit reg1bit_23 (.D(pu_3_cout), .WE(WE), .CK(CK), .Q(reg1bit_23_q));
  PU pu_27 (.A(A3c), .B(B0c), .Cin(1'b1), .S(pu_6_cout), .R(pu_27_r), .Cout(pu_27_cout));
  PU pu_28 (.A(reg1bit_24_q), .B(B1d), .Cin(pu_31_cout), .S(pu_10_cout), .R(pu_28_r), .Cout(pu_28_cout));
  PU pu_29 (.A(reg1bit_25_q), .B(B2e), .Cin(pu_32_cout), .S(pu_15_cout), .R(pu_29_r), .Cout(pu_29_cout));
  PU pu_30 (.A(reg1bit_26_q), .B(B3f), .Cin(pu_33_cout), .S(Q[0]), .R(R[3]), .Cout(pu_30_cout));
  reg1bit reg1bit_24 (.D(pu_27_r), .WE(WE), .CK(CK), .Q(reg1bit_24_q));
  reg1bit reg1bit_25 (.D(pu_28_r), .WE(WE), .CK(CK), .Q(reg1bit_25_q));
  reg1bit reg1bit_26 (.D(pu_29_r), .WE(WE), .CK(CK), .Q(reg1bit_26_q));
  reg1bit reg1bit_27 (.D(reg1bit_22_q), .WE(WE), .CK(CK), .Q(reg1bit_27_q));
  reg1bit reg1bit_28 (.D(reg1bit_23_q), .WE(WE), .CK(CK), .Q(reg1bit_28_q));
  reg1bit reg1bit_29 (.D(reg1bit_27_q), .WE(WE), .CK(CK), .Q(Q[5]));
  reg1bit reg1bit_30 (.D(reg1bit_28_q), .WE(WE), .CK(CK), .Q(reg1bit_30_q));
  reg1bit reg1bit_31 (.D(pu_6_cout), .WE(WE), .CK(CK), .Q(reg1bit_31_q));
  PU pu_31 (.A(A2d), .B(B0d), .Cin(1'b1), .S(pu_10_cout), .R(pu_31_r), .Cout(pu_31_cout));
  reg1bit reg1bit_32 (.D(pu_31_r), .WE(WE), .CK(CK), .Q(reg1bit_32_q));
  PU pu_32 (.A(reg1bit_32_q), .B(B1e), .Cin(pu_34_cout), .S(pu_15_cout), .R(pu_32_r), .Cout(pu_32_cout));
  reg1bit reg1bit_33 (.D(pu_32_r), .WE(WE), .CK(CK), .Q(reg1bit_33_q));
  PU pu_33 (.A(reg1bit_33_q), .B(B2f), .Cin(pu_35_cout), .S(Q[0]), .R(R[2]), .Cout(pu_33_cout));
  reg1bit reg1bit_34 (.D(reg1bit_31_q), .WE(WE), .CK(CK), .Q(reg1bit_34_q));
  reg1bit reg1bit_35 (.D(reg1bit_30_q), .WE(WE), .CK(CK), .Q(Q[4]));
  reg1bit reg1bit_36 (.D(reg1bit_34_q), .WE(WE), .CK(CK), .Q(Q[3]));
  reg1bit reg1bit_37 (.D(pu_10_cout), .WE(WE), .CK(CK), .Q(reg1bit_37_q));
  PU pu_34 (.A(A1e), .B(B0e), .Cin(1'b1), .S(pu_15_cout), .R(pu_34_r), .Cout(pu_34_cout));
  reg1bit reg1bit_38 (.D(pu_34_r), .WE(WE), .CK(CK), .Q(reg1bit_38_q));
  PU pu_35 (.A(reg1bit_38_q), .B(B1f), .Cin(pu_36_cout), .S(Q[0]), .R(R[1]), .Cout(pu_35_cout));
  reg1bit reg1bit_39 (.D(reg1bit_37_q), .WE(WE), .CK(CK), .Q(Q[2]));
  reg1bit reg1bit_40 (.D(pu_15_cout), .WE(WE), .CK(CK), .Q(Q[1]));
  PU pu_36 (.A(A0f), .B(B0f), .Cin(1'b1), .S(Q[0]), .R(R[0]), .Cout(pu_36_cout));
  reg1bit reg1bit_41 (.D(N[5]), .WE(WE), .CK(CK), .Q(A5a));
  reg1bit reg1bit_42 (.D(N[4]), .WE(WE), .CK(CK), .Q(reg1bit_42_q));
  reg1bit reg1bit_43 (.D(N[3]), .WE(WE), .CK(CK), .Q(reg1bit_43_q));
  reg1bit reg1bit_44 (.D(N[2]), .WE(WE), .CK(CK), .Q(reg1bit_44_q));
  reg1bit reg1bit_45 (.D(N[1]), .WE(WE), .CK(CK), .Q(reg1bit_45_q));
  reg1bit reg1bit_46 (.D(N[0]), .WE(WE), .CK(CK), .Q(reg1bit_46_q));
  reg1bit reg1bit_47 (.D(D[5]), .WE(WE), .CK(CK), .Q(B5a));
  reg1bit reg1bit_48 (.D(D[4]), .WE(WE), .CK(CK), .Q(B4a));
  reg1bit reg1bit_49 (.D(D[3]), .WE(WE), .CK(CK), .Q(B3a));
  reg1bit reg1bit_50 (.D(D[2]), .WE(WE), .CK(CK), .Q(B2a));
  reg1bit reg1bit_51 (.D(D[1]), .WE(WE), .CK(CK), .Q(B1a));
  reg1bit reg1bit_52 (.D(D[0]), .WE(WE), .CK(CK), .Q(B0a));
  reg1bit reg1bit_53 (.D(reg1bit_42_q), .WE(WE), .CK(CK), .Q(A4b));
  reg1bit reg1bit_54 (.D(reg1bit_43_q), .WE(WE), .CK(CK), .Q(reg1bit_54_q));
  reg1bit reg1bit_55 (.D(reg1bit_44_q), .WE(WE), .CK(CK), .Q(reg1bit_55_q));
  reg1bit reg1bit_56 (.D(reg1bit_45_q), .WE(WE), .CK(CK), .Q(reg1bit_56_q));
  reg1bit reg1bit_57 (.D(reg1bit_46_q), .WE(WE), .CK(CK), .Q(reg1bit_57_q));
  reg1bit reg1bit_58 (.D(B5a), .WE(WE), .CK(CK), .Q(B5b));
  reg1bit reg1bit_59 (.D(B4a), .WE(WE), .CK(CK), .Q(B4b));
  reg1bit reg1bit_60 (.D(B3a), .WE(WE), .CK(CK), .Q(B3b));
  reg1bit reg1bit_61 (.D(B2a), .WE(WE), .CK(CK), .Q(B2b));
  reg1bit reg1bit_62 (.D(B1a), .WE(WE), .CK(CK), .Q(B1b));
  reg1bit reg1bit_63 (.D(B0a), .WE(WE), .CK(CK), .Q(B0b));
  reg1bit reg1bit_64 (.D(reg1bit_54_q), .WE(WE), .CK(CK), .Q(A3c));
  reg1bit reg1bit_65 (.D(reg1bit_55_q), .WE(WE), .CK(CK), .Q(reg1bit_65_q));
  reg1bit reg1bit_66 (.D(reg1bit_56_q), .WE(WE), .CK(CK), .Q(reg1bit_66_q));
  reg1bit reg1bit_67 (.D(reg1bit_57_q), .WE(WE), .CK(CK), .Q(reg1bit_67_q));
  reg1bit reg1bit_68 (.D(B5b), .WE(WE), .CK(CK), .Q(B5c));
  reg1bit reg1bit_69 (.D(B4b), .WE(WE), .CK(CK), .Q(B4c));
  reg1bit reg1bit_70 (.D(B3b), .WE(WE), .CK(CK), .Q(B3c));
  reg1bit reg1bit_71 (.D(B2b), .WE(WE), .CK(CK), .Q(B2c));
  reg1bit reg1bit_72 (.D(B1b), .WE(WE), .CK(CK), .Q(B1c));
  reg1bit reg1bit_73 (.D(B0b), .WE(WE), .CK(CK), .Q(B0c));
  reg1bit reg1bit_74 (.D(reg1bit_65_q), .WE(WE), .CK(CK), .Q(A2d));
  reg1bit reg1bit_75 (.D(reg1bit_66_q), .WE(WE), .CK(CK), .Q(reg1bit_75_q));
  reg1bit reg1bit_76 (.D(reg1bit_67_q), .WE(WE), .CK(CK), .Q(reg1bit_76_q));
  reg1bit reg1bit_77 (.D(B5c), .WE(WE), .CK(CK), .Q(B5d));
  reg1bit reg1bit_78 (.D(B4c), .WE(WE), .CK(CK), .Q(B4d));
  reg1bit reg1bit_79 (.D(B3c), .WE(WE), .CK(CK), .Q(B3d));
  reg1bit reg1bit_80 (.D(B2c), .WE(WE), .CK(CK), .Q(B2d));
  reg1bit reg1bit_81 (.D(B1c), .WE(WE), .CK(CK), .Q(B1d));
  reg1bit reg1bit_82 (.D(B0c), .WE(WE), .CK(CK), .Q(B0d));
  reg1bit reg1bit_83 (.D(reg1bit_75_q), .WE(WE), .CK(CK), .Q(A1e));
  reg1bit reg1bit_84 (.D(reg1bit_76_q), .WE(WE), .CK(CK), .Q(reg1bit_84_q));
  reg1bit reg1bit_85 (.D(B5d), .WE(WE), .CK(CK), .Q(B5e));
  reg1bit reg1bit_86 (.D(B4d), .WE(WE), .CK(CK), .Q(B4e));
  reg1bit reg1bit_87 (.D(B3d), .WE(WE), .CK(CK), .Q(B3e));
  reg1bit reg1bit_88 (.D(B2d), .WE(WE), .CK(CK), .Q(B2e));
  reg1bit reg1bit_89 (.D(B1d), .WE(WE), .CK(CK), .Q(B1e));
  reg1bit reg1bit_90 (.D(B0d), .WE(WE), .CK(CK), .Q(B0e));
  reg1bit reg1bit_91 (.D(reg1bit_84_q), .WE(WE), .CK(CK), .Q(A0f));
  reg1bit reg1bit_92 (.D(B5e), .WE(WE), .CK(CK), .Q(B5f));
  reg1bit reg1bit_93 (.D(B4e), .WE(WE), .CK(CK), .Q(B4f));
  reg1bit reg1bit_94 (.D(B3e), .WE(WE), .CK(CK), .Q(B3f));
  reg1bit reg1bit_95 (.D(B2e), .WE(WE), .CK(CK), .Q(B2f));
  reg1bit reg1bit_96 (.D(B1e), .WE(WE), .CK(CK), .Q(B1f));
  reg1bit reg1bit_97 (.D(B0e), .WE(WE), .CK(CK), .Q(B0f));

  // Other names for the same wires on the sheet: B0 = D[0]; B1 = D[1]; B2 = D[2]; B3 = D[3]; B4 = D[4]; B5 = D[5];
  //   A0 = N[0]; A1 = N[1]; A2 = N[2]; A3 = N[3]; A4 = N[4]; A5 = N[5]

  // Notes on the sheet:
  //   Attention, votre version de Logisim
  //   ne contient pas de tracker. Si vous
  //   enregistrez votre projet, toutes les
  //   informations du tracker seront
  //   définitivement effacées.
endmodule

module PU (
  input  A,
  input  B,
  input  Cin,
  input  S,
  output R,
  output Cout
);

  wire adder_1_out, not_1_out;

  not not_1 (not_1_out, B);
  Adder #(.width(1)) adder_1 (.a(A), .b(not_1_out), .out(adder_1_out), .cin(Cin), .cout(Cout));
  Multiplexer #(.enable("false")) multiplexer_1 (.in0(A), .in1(adder_1_out), .out(R), .sel(S));

  // Notes on the sheet:
  //   Attention, votre version de Logisim
  //   ne contient pas de tracker. Si vous
  //   enregistrez votre projet, toutes les
  //   informations du tracker seront
  //   définitivement effacées.
endmodule

module reg1bit (
  input  D,
  input  WE,
  input  CK,
  output Q
);

  Register #(.width(1)) register_1 (.D(D), .en(WE), .clk(CK), .Q(Q));  // open: clr

  // Notes on the sheet:
  //   Attention, votre version de Logisim
  //   ne contient pas de tracker. Si vous
  //   enregistrez votre projet, toutes les
  //   informations du tracker seront
  //   définitivement effacées.
endmodule
