// Logisim project 6-bit_Pipelined_Wallace_Tree_Unsigned_Multiplier.circ as structural Verilog: 5 circuits, main circuit main
module main (
  output halt,
  output [5:0] A,
  output [5:0] B,
  output [11:0] P
);

  wire clock_1_out, comparator_1_eq, d_ff_1_q;
  wire [11:0] bit_extender_1_out, bit_extender_2_out, multiplier_1_out, random_1_out;

  Counter #(.width(12), .max('hfff)) counter_1 (.clk(clock_1_out), .carry(halt));  // open: clr, load, up, count, D, Q
  Clock clock_1 (.out(clock_1_out));
  Random #(.width(12)) random_1 (.next(d_ff_1_q), .clk(clock_1_out), .out(random_1_out));  // open: clr
  RAM #(.addrWidth(12), .dataWidth(1), .trigger("falling"), .databus("bibus")) ram_1 (
    .addr(random_1_out), .we(d_ff_1_q), .clk(clock_1_out), .din(1'b1));  // open: oe, dout
  // Probe on A
  mycircuit mycircuit_1 (
    .A(random_1_out[5:0]), .B(random_1_out[11:6]), .CK(clock_1_out), .WE(d_ff_1_q), .AO(A), .BO(B), .P(P));
  // Probe on B
  assign bit_extender_1_out = {{6{1'b0}}, A};  // Bit_Extender bit_extender_1
  assign bit_extender_2_out = {{6{1'b0}}, B};  // Bit_Extender bit_extender_2
  Multiplier #(.width(12)) multiplier_1 (
    .a(bit_extender_1_out), .b(bit_extender_2_out), .out(multiplier_1_out));  // open: cin, cout
  // Probe on multiplier_1_out
  // Probe on P
  Comparator #(.width(12)) comparator_1 (.a(P), .b(multiplier_1_out), .eq(comparator_1_eq));  // open: gt, lt
  D_Flip_Flop #(.trigger("falling")) d_ff_1 (
    .D(comparator_1_eq), .clk(clock_1_out), .Q(d_ff_1_q));  // open: Qn, preset, reset

  // Notes on the sheet:
  //   Attention, votre version de Logisim
  //   ne contient pas de tracker. Si vous
  //   enregistrez votre projet, toutes les
  //   informations du tracker seront
  //   définitivement effacées.
endmodule

module mycircuit (
  input  [5:0] A,
  input  [5:0] B,
  input  CK,
  input  WE,
  output [5:0] AO,
  output [5:0] BO,
  output [11:0] P
);

  wire A0B0, A0B1, A0B2, A0B3, A0B4, A0B5, A1_cout, A1_s, A1B0, A1B1, A1B2, A1B3, A1B4, A1B5, A2_cout,
       A2_sum, A2B0, A2B1, A2B2, A2B3, A2B4, A2B5, A3_cout, A3_sum, A3B0, A3B1, A3B2, A3B3, A3B4, A3B5,
       A4_cout, A4_sum, A4B0, A4B1, A4B2, A4B3, A4B4, A4B5, A5_cout, A5_sum, A5B0, A5B1, A5B2, A5B3, A5B4,
       A5B5, A6_cout, A6_sum, A7_cout, A7_sum, A8_cout, A8_sum, A9_cout, A9_s, A13_cout, A13_s, A14_cout,
       A14_sum, A15_cout, A15_sum, A16_cout, A16_sum, A17_cout, A17_sum, A18_cout, A18_sum, A19_cout, A19_s,
       A20_cout, A20_s, A21_cout, A21_s, A22_cout, A22_s, A23_cout, A23_s, A24_cout, A24_sum, A25_cout,
       A25_sum, A26_cout, A26_sum, A27_cout, A27_s, A28_cout, A28_s, A29_cout, A29_s, C10, C11, C12, C21,
       C22, C23, C24, C25, C26, C27, C28, C29, reg1bit_1_q, reg1bit_2_q, reg1bit_3_q, reg1bit_4_q,
       reg1bit_5_q, reg1bit_6_q, reg1bit_7_q, reg1bit_8_q, reg1bit_9_q, reg1bit_10_q, reg1bit_11_q,
       reg1bit_12_q, reg1bit_13_q, reg1bit_14_q, reg1bit_15_q, reg1bit_16_q, reg1bit_17_q, reg1bit_18_q,
       reg1bit_19_q, reg1bit_20_q, reg1bit_21_q, reg1bit_22_q, reg1bit_23_q, reg1bit_24_q, reg1bit_25_q,
       reg1bit_26_q, reg1bit_27_q, reg1bit_28_q, reg1bit_29_q, reg1bit_30_q, reg1bit_31_q, reg1bit_32_q,
       reg1bit_33_q, reg1bit_34_q, reg1bit_35_q, reg1bit_36_q, reg1bit_49_q, reg1bit_50_q, reg1bit_52_q,
       reg1bit_53_q, reg1bit_55_q, reg1bit_56_q, reg1bit_58_q, reg1bit_59_q, reg1bit_61_q, reg1bit_62_q,
       reg1bit_64_q, reg1bit_65_q, reg1bit_67_q, reg1bit_68_q, reg1bit_69_q, reg1bit_71_q, reg1bit_72_q,
       reg1bit_73_q, reg1bit_74_q, reg1bit_76_q, reg1bit_77_q, reg1bit_78_q, reg1bit_80_q, reg1bit_81_q,
       reg1bit_82_q, reg1bit_83_q, reg1bit_85_q, reg1bit_86_q, reg1bit_87_q, reg1bit_89_q, reg1bit_90_q,
       reg1bit_91_q, reg1bit_92_q, reg1bit_94_q, reg1bit_95_q, reg1bit_97_q, reg1bit_98_q, reg1bit_99_q,
       reg1bit_101_q, reg1bit_102_q, reg1bit_103_q, reg1bit_105_q, reg1bit_106_q, reg1bit_108_q,
       reg1bit_109_q, reg1bit_110_q, reg1bit_111_q, reg1bit_112_q, reg1bit_113_q, reg1bit_114_q,
       reg1bit_115_q, reg1bit_117_q, reg1bit_118_q, reg1bit_119_q, reg1bit_120_q, S10, S11, S12, S23, S24,
       S25, S26, S27, S28, S29;
  wire [7:0] adder_1_out;

  reg1bit reg1bit_1 (.D(A[0]), .WE(WE), .CK(CK), .Q(reg1bit_1_q));
  reg1bit reg1bit_2 (.D(A[1]), .WE(WE), .CK(CK), .Q(reg1bit_2_q));
  reg1bit reg1bit_3 (.D(A[2]), .WE(WE), .CK(CK), .Q(reg1bit_3_q));
  reg1bit reg1bit_4 (.D(A[3]), .WE(WE), .CK(CK), .Q(reg1bit_4_q));
  reg1bit reg1bit_5 (.D(A[4]), .WE(WE), .CK(CK), .Q(reg1bit_5_q));
  reg1bit reg1bit_6 (.D(A[5]), .WE(WE), .CK(CK), .Q(reg1bit_6_q));
  reg1bit reg1bit_7 (.D(B[0]), .WE(WE), .CK(CK), .Q(reg1bit_7_q));
  reg1bit reg1bit_8 (.D(B[1]), .WE(WE), .CK(CK), .Q(reg1bit_8_q));
  reg1bit reg1bit_9 (.D(B[2]), .WE(WE), .CK(CK), .Q(reg1bit_9_q));
  reg1bit reg1bit_10 (.D(B[3]), .WE(WE), .CK(CK), .Q(reg1bit_10_q));
  reg1bit reg1bit_11 (.D(B[4]), .WE(WE), .CK(CK), .Q(reg1bit_11_q));
  reg1bit reg1bit_12 (.D(B[5]), .WE(WE), .CK(CK), .Q(reg1bit_12_q));
  reg1bit reg1bit_13 (.D(reg1bit_1_q), .WE(WE), .CK(CK), .Q(reg1bit_13_q));
  reg1bit reg1bit_14 (.D(reg1bit_2_q), .WE(WE), .CK(CK), .Q(reg1bit_14_q));
  reg1bit reg1bit_15 (.D(reg1bit_3_q), .WE(WE), .CK(CK), .Q(reg1bit_15_q));
  reg1bit reg1bit_16 (.D(reg1bit_4_q), .WE(WE), .CK(CK), .Q(reg1bit_16_q));
  reg1bit reg1bit_17 (.D(reg1bit_5_q), .WE(WE), .CK(CK), .Q(reg1bit_17_q));
  reg1bit reg1bit_18 (.D(reg1bit_6_q), .WE(WE), .CK(CK), .Q(reg1bit_18_q));
  reg1bit reg1bit_19 (.D(reg1bit_7_q), .WE(WE), .CK(CK), .Q(reg1bit_19_q));
  reg1bit reg1bit_20 (.D(reg1bit_8_q), .WE(WE), .CK(CK), .Q(reg1bit_20_q));
  reg1bit reg1bit_21 (.D(reg1bit_9_q), .WE(WE), .CK(CK), .Q(reg1bit_21_q));
  reg1bit reg1bit_22 (.D(reg1bit_10_q), .WE(WE), .CK(CK), .Q(reg1bit_22_q));
  reg1bit reg1bit_23 (.D(reg1bit_11_q), .WE(WE), .CK(CK), .Q(reg1bit_23_q));
  reg1bit reg1bit_24 (.D(reg1bit_12_q), .WE(WE), .CK(CK), .Q(reg1bit_24_q));
  reg1bit reg1bit_25 (.D(reg1bit_13_q), .WE(WE), .CK(CK), .Q(reg1bit_25_q));
  reg1bit reg1bit_26 (.D(reg1bit_14_q), .WE(WE), .CK(CK), .Q(reg1bit_26_q));
  reg1bit reg1bit_27 (.D(reg1bit_15_q), .WE(WE), .CK(CK), .Q(reg1bit_27_q));
  reg1bit reg1bit_28 (.D(reg1bit_16_q), .WE(WE), .CK(CK), .Q(reg1bit_28_q));
  reg1bit reg1bit_29 (.D(reg1bit_17_q), .WE(WE), .CK(CK), .Q(reg1bit_29_q));
  reg1bit reg1bit_30 (.D(reg1bit_18_q), .WE(WE), .CK(CK), .Q(reg1bit_30_q));
  reg1bit reg1bit_31 (.D(reg1bit_19_q), .WE(WE), .CK(CK), .Q(reg1bit_31_q));
  reg1bit reg1bit_32 (.D(reg1bit_20_q), .WE(WE), .CK(CK), .Q(reg1bit_32_q));
  reg1bit reg1bit_33 (.D(reg1bit_21_q), .WE(WE), .CK(CK), .Q(reg1bit_33_q));
  reg1bit reg1bit_34 (.D(reg1bit_22_q), .WE(WE), .CK(CK), .Q(reg1bit_34_q));
  reg1bit reg1bit_35 (.D(reg1bit_23_q), .WE(WE), .CK(CK), .Q(reg1bit_35_q));
  reg1bit reg1bit_36 (.D(reg1bit_24_q), .WE(WE), .CK(CK), .Q(reg1bit_36_q));
  HA A12 (.A(A2B4), .B(A1B5), .S(S12), .Cout(C12));
  reg1bit reg1bit_37 (.D(reg1bit_25_q), .WE(WE), .CK(CK), .Q(AO[0]));
  reg1bit reg1bit_38 (.D(reg1bit_26_q), .WE(WE), .CK(CK), .Q(AO[1]));
  reg1bit reg1bit_39 (.D(reg1bit_27_q), .WE(WE), .CK(CK), .Q(AO[2]));
  reg1bit reg1bit_40 (.D(reg1bit_28_q), .WE(WE), .CK(CK), .Q(AO[3]));
  reg1bit reg1bit_41 (.D(reg1bit_29_q), .WE(WE), .CK(CK), .Q(AO[4]));
  reg1bit reg1bit_42 (.D(reg1bit_30_q), .WE(WE), .CK(CK), .Q(AO[5]));
  reg1bit reg1bit_43 (.D(reg1bit_31_q), .WE(WE), .CK(CK), .Q(BO[0]));
  reg1bit reg1bit_44 (.D(reg1bit_32_q), .WE(WE), .CK(CK), .Q(BO[1]));
  reg1bit reg1bit_45 (.D(reg1bit_33_q), .WE(WE), .CK(CK), .Q(BO[2]));
  reg1bit reg1bit_46 (.D(reg1bit_34_q), .WE(WE), .CK(CK), .Q(BO[3]));
  reg1bit reg1bit_47 (.D(reg1bit_35_q), .WE(WE), .CK(CK), .Q(BO[4]));
  reg1bit reg1bit_48 (.D(reg1bit_36_q), .WE(WE), .CK(CK), .Q(BO[5]));
  FA A11 (.A(A2B3), .B(A1B4), .Cin(A0B5), .Sum(S11), .Cout(C11));
  HA A10 (.A(A1B3), .B(A0B4), .S(S10), .Cout(C10));
  reg1bit reg1bit_49 (.D(A5B5), .WE(WE), .CK(CK), .Q(reg1bit_49_q));
  reg1bit reg1bit_50 (.D(A21_cout), .WE(WE), .CK(CK), .Q(reg1bit_50_q));
  reg1bit reg1bit_51 (.D(reg1bit_50_q), .WE(WE), .CK(CK), .Q(C21));
  reg1bit reg1bit_52 (.D(A9_cout), .WE(WE), .CK(CK), .Q(reg1bit_52_q));
  HA A21 (.A(reg1bit_52_q), .B(reg1bit_49_q), .S(A21_s), .Cout(A21_cout));
  reg1bit reg1bit_53 (.D(A21_s), .WE(WE), .CK(CK), .Q(reg1bit_53_q));
  reg1bit reg1bit_54 (.D(A29_cout), .WE(WE), .CK(CK), .Q(C29));
  HA A9 (.A(A5B4), .B(A4B5), .S(A9_s), .Cout(A9_cout));
  reg1bit reg1bit_55 (.D(A9_s), .WE(WE), .CK(CK), .Q(reg1bit_55_q));
  reg1bit reg1bit_56 (.D(A20_cout), .WE(WE), .CK(CK), .Q(reg1bit_56_q));
  HA A29 (.A(reg1bit_56_q), .B(reg1bit_53_q), .S(A29_s), .Cout(A29_cout));
  reg1bit reg1bit_57 (.D(A29_s), .WE(WE), .CK(CK), .Q(S29));
  reg1bit reg1bit_58 (.D(A8_cout), .WE(WE), .CK(CK), .Q(reg1bit_58_q));
  HA A20 (.A(reg1bit_58_q), .B(reg1bit_55_q), .S(A20_s), .Cout(A20_cout));
  reg1bit reg1bit_59 (.D(A20_s), .WE(WE), .CK(CK), .Q(reg1bit_59_q));
  reg1bit reg1bit_60 (.D(A28_cout), .WE(WE), .CK(CK), .Q(C28));
  FA A8 (.A(A5B3), .B(A4B4), .Cin(A3B5), .Sum(A8_sum), .Cout(A8_cout));
  reg1bit reg1bit_61 (.D(A8_sum), .WE(WE), .CK(CK), .Q(reg1bit_61_q));
  reg1bit reg1bit_62 (.D(A19_cout), .WE(WE), .CK(CK), .Q(reg1bit_62_q));
  HA A28 (.A(reg1bit_62_q), .B(reg1bit_59_q), .S(A28_s), .Cout(A28_cout));
  reg1bit reg1bit_63 (.D(A28_s), .WE(WE), .CK(CK), .Q(S28));
  reg1bit reg1bit_64 (.D(A7_cout), .WE(WE), .CK(CK), .Q(reg1bit_64_q));
  HA A19 (.A(reg1bit_64_q), .B(reg1bit_61_q), .S(A19_s), .Cout(A19_cout));
  reg1bit reg1bit_65 (.D(A19_s), .WE(WE), .CK(CK), .Q(reg1bit_65_q));
  reg1bit reg1bit_66 (.D(A27_cout), .WE(WE), .CK(CK), .Q(C27));
  FA A7 (.A(A5B2), .B(A4B3), .Cin(A3B4), .Sum(A7_sum), .Cout(A7_cout));
  reg1bit reg1bit_67 (.D(A7_sum), .WE(WE), .CK(CK), .Q(reg1bit_67_q));
  reg1bit reg1bit_68 (.D(C12), .WE(WE), .CK(CK), .Q(reg1bit_68_q));
  reg1bit reg1bit_69 (.D(A18_cout), .WE(WE), .CK(CK), .Q(reg1bit_69_q));
  HA A27 (.A(reg1bit_69_q), .B(reg1bit_65_q), .S(A27_s), .Cout(A27_cout));
  reg1bit reg1bit_70 (.D(A27_s), .WE(WE), .CK(CK), .Q(S27));
  reg1bit reg1bit_71 (.D(A6_cout), .WE(WE), .CK(CK), .Q(reg1bit_71_q));
  FA A18 (.A(reg1bit_71_q), .B(reg1bit_67_q), .Cin(reg1bit_68_q), .Sum(A18_sum), .Cout(A18_cout));
  reg1bit reg1bit_72 (.D(A18_sum), .WE(WE), .CK(CK), .Q(reg1bit_72_q));
  reg1bit reg1bit_73 (.D(A2B5), .WE(WE), .CK(CK), .Q(reg1bit_73_q));
  reg1bit reg1bit_74 (.D(reg1bit_73_q), .WE(WE), .CK(CK), .Q(reg1bit_74_q));
  reg1bit reg1bit_75 (.D(A26_cout), .WE(WE), .CK(CK), .Q(C26));
  FA A6 (.A(A5B1), .B(A4B2), .Cin(A3B3), .Sum(A6_sum), .Cout(A6_cout));
  reg1bit reg1bit_76 (.D(A6_sum), .WE(WE), .CK(CK), .Q(reg1bit_76_q));
  reg1bit reg1bit_77 (.D(C11), .WE(WE), .CK(CK), .Q(reg1bit_77_q));
  reg1bit reg1bit_78 (.D(A17_cout), .WE(WE), .CK(CK), .Q(reg1bit_78_q));
  FA A26 (.A(reg1bit_78_q), .B(reg1bit_72_q), .Cin(reg1bit_74_q), .Sum(A26_sum), .Cout(A26_cout));
  reg1bit reg1bit_79 (.D(A26_sum), .WE(WE), .CK(CK), .Q(S26));
  reg1bit reg1bit_80 (.D(A5_cout), .WE(WE), .CK(CK), .Q(reg1bit_80_q));
  FA A17 (.A(reg1bit_80_q), .B(reg1bit_76_q), .Cin(reg1bit_77_q), .Sum(A17_sum), .Cout(A17_cout));
  reg1bit reg1bit_81 (.D(A17_sum), .WE(WE), .CK(CK), .Q(reg1bit_81_q));
  reg1bit reg1bit_82 (.D(S12), .WE(WE), .CK(CK), .Q(reg1bit_82_q));
  reg1bit reg1bit_83 (.D(reg1bit_82_q), .WE(WE), .CK(CK), .Q(reg1bit_83_q));
  reg1bit reg1bit_84 (.D(A25_cout), .WE(WE), .CK(CK), .Q(C25));
  FA A5 (.A(A5B0), .B(A4B1), .Cin(A3B2), .Sum(A5_sum), .Cout(A5_cout));
  reg1bit reg1bit_85 (.D(A5_sum), .WE(WE), .CK(CK), .Q(reg1bit_85_q));
  reg1bit reg1bit_86 (.D(C10), .WE(WE), .CK(CK), .Q(reg1bit_86_q));
  reg1bit reg1bit_87 (.D(A16_cout), .WE(WE), .CK(CK), .Q(reg1bit_87_q));
  FA A25 (.A(reg1bit_87_q), .B(reg1bit_81_q), .Cin(reg1bit_83_q), .Sum(A25_sum), .Cout(A25_cout));
  reg1bit reg1bit_88 (.D(A25_sum), .WE(WE), .CK(CK), .Q(S25));
  reg1bit reg1bit_89 (.D(A4_cout), .WE(WE), .CK(CK), .Q(reg1bit_89_q));
  FA A16 (.A(reg1bit_89_q), .B(reg1bit_85_q), .Cin(reg1bit_86_q), .Sum(A16_sum), .Cout(A16_cout));
  reg1bit reg1bit_90 (.D(A16_sum), .WE(WE), .CK(CK), .Q(reg1bit_90_q));
  reg1bit reg1bit_91 (.D(S11), .WE(WE), .CK(CK), .Q(reg1bit_91_q));
  reg1bit reg1bit_92 (.D(reg1bit_91_q), .WE(WE), .CK(CK), .Q(reg1bit_92_q));
  reg1bit reg1bit_93 (.D(A24_cout), .WE(WE), .CK(CK), .Q(C24));
  FA A4 (.A(A4B0), .B(A3B1), .Cin(A2B2), .Sum(A4_sum), .Cout(A4_cout));
  reg1bit reg1bit_94 (.D(A4_sum), .WE(WE), .CK(CK), .Q(reg1bit_94_q));
  reg1bit reg1bit_95 (.D(A15_cout), .WE(WE), .CK(CK), .Q(reg1bit_95_q));
  FA A24 (.A(reg1bit_95_q), .B(reg1bit_90_q), .Cin(reg1bit_92_q), .Sum(A24_sum), .Cout(A24_cout));
  reg1bit reg1bit_96 (.D(A24_sum), .WE(WE), .CK(CK), .Q(S24));
  reg1bit reg1bit_97 (.D(S10), .WE(WE), .CK(CK), .Q(reg1bit_97_q));
  reg1bit reg1bit_98 (.D(A3_cout), .WE(WE), .CK(CK), .Q(reg1bit_98_q));
  FA A15 (.A(reg1bit_98_q), .B(reg1bit_94_q), .Cin(reg1bit_97_q), .Sum(A15_sum), .Cout(A15_cout));
  reg1bit reg1bit_99 (.D(A15_sum), .WE(WE), .CK(CK), .Q(reg1bit_99_q));
  reg1bit reg1bit_100 (.D(A23_cout), .WE(WE), .CK(CK), .Q(C23));
  FA A3 (.A(A3B0), .B(A2B1), .Cin(A1B2), .Sum(A3_sum), .Cout(A3_cout));
  reg1bit reg1bit_101 (.D(A3_sum), .WE(WE), .CK(CK), .Q(reg1bit_101_q));
  reg1bit reg1bit_102 (.D(A0B3), .WE(WE), .CK(CK), .Q(reg1bit_102_q));
  reg1bit reg1bit_103 (.D(A14_cout), .WE(WE), .CK(CK), .Q(reg1bit_103_q));
  HA A23 (.A(reg1bit_103_q), .B(reg1bit_99_q), .S(A23_s), .Cout(A23_cout));
  reg1bit reg1bit_104 (.D(A23_s), .WE(WE), .CK(CK), .Q(S23));
  reg1bit reg1bit_105 (.D(A2_cout), .WE(WE), .CK(CK), .Q(reg1bit_105_q));
  FA A14 (.A(reg1bit_105_q), .B(reg1bit_101_q), .Cin(reg1bit_102_q), .Sum(A14_sum), .Cout(A14_cout));
  reg1bit reg1bit_106 (.D(A14_sum), .WE(WE), .CK(CK), .Q(reg1bit_106_q));
  reg1bit reg1bit_107 (.D(A22_cout), .WE(WE), .CK(CK), .Q(C22));
  FA A2 (.A(A2B0), .B(A1B1), .Cin(A0B2), .Sum(A2_sum), .Cout(A2_cout));
  reg1bit reg1bit_108 (.D(A2_sum), .WE(WE), .CK(CK), .Q(reg1bit_108_q));
  reg1bit reg1bit_109 (.D(A13_cout), .WE(WE), .CK(CK), .Q(reg1bit_109_q));
  HA A22 (.A(reg1bit_109_q), .B(reg1bit_106_q), .S(A22_s), .Cout(A22_cout));
  HA A1 (.A(A1B0), .B(A0B1), .S(A1_s), .Cout(A1_cout));
  reg1bit reg1bit_110 (.D(A1_cout), .WE(WE), .CK(CK), .Q(reg1bit_110_q));
  HA A13 (.A(reg1bit_110_q), .B(reg1bit_108_q), .S(A13_s), .Cout(A13_cout));
  reg1bit reg1bit_111 (.D(A22_s), .WE(WE), .CK(CK), .Q(reg1bit_111_q));
  reg1bit reg1bit_112 (.D(A0B0), .WE(WE), .CK(CK), .Q(reg1bit_112_q));
  reg1bit reg1bit_113 (.D(A1_s), .WE(WE), .CK(CK), .Q(reg1bit_113_q));
  reg1bit reg1bit_114 (.D(A13_s), .WE(WE), .CK(CK), .Q(reg1bit_114_q));
  reg1bit reg1bit_115 (.D(reg1bit_114_q), .WE(WE), .CK(CK), .Q(reg1bit_115_q));
  reg1bit reg1bit_116 (.D(reg1bit_111_q), .WE(WE), .CK(CK), .Q(P[3]));
  reg1bit reg1bit_117 (.D(reg1bit_112_q), .WE(WE), .CK(CK), .Q(reg1bit_117_q));
  reg1bit reg1bit_118 (.D(reg1bit_113_q), .WE(WE), .CK(CK), .Q(reg1bit_118_q));
  reg1bit reg1bit_119 (.D(reg1bit_117_q), .WE(WE), .CK(CK), .Q(reg1bit_119_q));
  reg1bit reg1bit_120 (.D(reg1bit_118_q), .WE(WE), .CK(CK), .Q(reg1bit_120_q));
  reg1bit reg1bit_121 (.D(reg1bit_115_q), .WE(WE), .CK(CK), .Q(P[2]));
  reg1bit reg1bit_122 (.D(reg1bit_119_q), .WE(WE), .CK(CK), .Q(P[0]));
  reg1bit reg1bit_123 (.D(reg1bit_120_q), .WE(WE), .CK(CK), .Q(P[1]));
  and and_1 (A5B5, B[5], A[5]);
  and and_2 (A5B4, B[4], A[5]);
  and and_3 (A4B5, B[5], A[4]);
  Adder adder_1 (
    .a({C29, C28, C27, C26, C25, C24, C23, C22}), .b({C21, S29, S28, S27, S26, S25, S24, S23}),
    .out(adder_1_out));  // open: cin, cout
  and and_4 (A5B3, B[3], A[5]);
  and and_5 (A4B4, B[4], A[4]);
  and and_6 (A3B5, B[5], A[3]);
  Register register_1 (.D(adder_1_out), .en(WE), .clk(CK), .Q(P[11:4]));  // open: clr
  and and_7 (A5B2, B[2], A[5]);
  and and_8 (A4B3, B[3], A[4]);
  and and_9 (A3B4, B[4], A[3]);
  and and_10 (A2B5, B[5], A[2]);
  and and_11 (A5B1, B[1], A[5]);
  and and_12 (A4B2, B[2], A[4]);
  and and_13 (A3B3, B[3], A[3]);
  and and_14 (A2B4, B[4], A[2]);
  and and_15 (A1B5, B[5], A[1]);
  and and_16 (A5B0, B[0], A[5]);
  and and_17 (A4B1, B[1], A[4]);
  and and_18 (A3B2, B[2], A[3]);
  and and_19 (A2B3, B[3], A[2]);
  and and_20 (A1B4, B[4], A[1]);
  and and_21 (A0B5, B[5], A[0]);
  and and_22 (A4B0, B[0], A[4]);
  and and_23 (A3B1, B[1], A[3]);
  and and_24 (A2B2, B[2], A[2]);
  and and_25 (A1B3, B[3], A[1]);
  and and_26 (A0B4, B[4], A[0]);
  and and_27 (A3B0, B[0], A[3]);
  and and_28 (A2B1, B[1], A[2]);
  and and_29 (A1B2, B[2], A[1]);
  and and_30 (A0B3, B[3], A[0]);
  and and_31 (A2B0, B[0], A[2]);
  and and_32 (A1B1, B[1], A[1]);
  and and_33 (A0B2, B[2], A[0]);
  and and_34 (A1B0, B[0], A[1]);
  and and_35 (A0B1, B[1], A[0]);
  and and_36 (A0B0, B[0], A[0]);

  // Notes on the sheet:
  //   Attention, votre version de Logisim
  //   ne contient pas de tracker. Si vous
  //   enregistrez votre projet, toutes les
  //   informations du tracker seront
  //   définitivement effacées.
endmodule

module HA (
  input  A,
  input  B,
  output S,
  output Cout
);

  xor xor_1 (S, A, B);
  and and_1 (Cout, A, B);

  // Notes on the sheet:
  //   Attention, votre version de Logisim
  //   ne contient pas de tracker. Si vous
  //   enregistrez votre projet, toutes les
  //   informations du tracker seront
  //   définitivement effacées.
endmodule

module FA (
  input  A,
  input  B,
  input  Cin,
  output Sum,
  output Cout
);

  wire and_1_out, and_2_out, xor_1_out;

  and and_1 (and_1_out, A, B);
  and and_2 (and_2_out, xor_1_out, Cin);
  or or_1 (Cout, and_1_out, and_2_out);
  xor xor_1 (xor_1_out, A, B);
  xor xor_2 (Sum, xor_1_out, Cin);

  // Notes on the sheet:
  //   Attention, votre version de Logisim
  //   ne contient pas de tracker. Si vous
  //   enregistrez votre projet, toutes les
  //   informations du tracker seront
  //   définitivement effacées.
endmodule

module reg1bit (
  input  D,
  input  WE,
  input  CK,
  output Q
);

  Register #(.width(1)) register_1 (.D(D), .en(WE), .clk(CK), .Q(Q));  // open: clr

  // Notes on the sheet:
  //   Attention, votre version de Logisim
  //   ne contient pas de tracker. Si vous
  //   enregistrez votre projet, toutes les
  //   informations du tracker seront
  //   définitivement effacées.
endmodule
